// Logisim project 4bitAddrReg.circ as structural Verilog: 1 circuit, main circuit 4BitAddrReg
module _4BitAddrReg (
  input  [3:0] Input,
  input  [1:0] Address,
  input  CLK,
  input  _0,
  output [3:0] Output
);

  wire demultiplexer_1_out0, demultiplexer_1_out1, demultiplexer_1_out2, demultiplexer_1_out3;

  Demultiplexer #(.select(2), .enable("false")) demultiplexer_1 (
    .out0(demultiplexer_1_out0), .out1(demultiplexer_1_out1), .out2(demultiplexer_1_out2),
    .out3(demultiplexer_1_out3), .in(CLK), .sel(Address));
  D_Flip_Flop d_ff_1 (.clk(demultiplexer_1_out0), .D(Input[3]), .Q(Output[3]), .reset(_0));  // open: Qn, preset, en
  D_Flip_Flop d_ff_2 (.clk(demultiplexer_1_out1), .D(Input[2]), .Q(Output[2]), .reset(_0));  // open: Qn, preset, en
  D_Flip_Flop d_ff_3 (.clk(demultiplexer_1_out2), .D(Input[1]), .Q(Output[1]), .reset(_0));  // open: Qn, preset, en
  D_Flip_Flop d_ff_4 (.clk(demultiplexer_1_out3), .D(Input[0]), .Q(Output[0]), .reset(_0));  // open: Qn, preset, en
endmodule
