// Logisim project 64bitAddrReg.circ as structural Verilog: 1 circuit, main circuit 64bitAddrReg
module _64bitAddrReg (
  input  Input,
  input  RST,
  input  [5:0] Address,
  input  CLK,
  output Output
);

  wire demultiplexer_2_out0, demultiplexer_2_out1, demultiplexer_2_out2, demultiplexer_2_out3,
       demultiplexer_2_out4, demultiplexer_2_out5, demultiplexer_2_out6, demultiplexer_2_out7;
  wire [2:0] not_1_out;
  wire [7:0] demultiplexer_1_out0, demultiplexer_1_out1, demultiplexer_1_out2, demultiplexer_1_out3,
       demultiplexer_1_out4, demultiplexer_1_out5, demultiplexer_1_out6, demultiplexer_1_out7,
       multiplexer_1_out, n8bitaddrreg_1_output, n8bitaddrreg_2_output, n8bitaddrreg_3_output,
       n8bitaddrreg_4_output, n8bitaddrreg_5_output, n8bitaddrreg_6_output, n8bitaddrreg_7_output,
       n8bitaddrreg_8_output, shifter_1_out;

  Shifter #(.shift("lr")) shifter_1 (.in({Input, {7{1'b0}}}), .\dist (Address[2:0]), .out(shifter_1_out));
  Demultiplexer #(.select(3), .width(8), .enable("false")) demultiplexer_1 (
    .out0(demultiplexer_1_out0), .out1(demultiplexer_1_out1), .out2(demultiplexer_1_out2),
    .out3(demultiplexer_1_out3), .out4(demultiplexer_1_out4), .out5(demultiplexer_1_out5),
    .out6(demultiplexer_1_out6), .out7(demultiplexer_1_out7), .in(shifter_1_out), .sel(Address[5:3]));
  _8bitAddrReg u_8bitaddrreg_1 (
    .Input(demultiplexer_1_out0), .Address(Address[2:0]), .CLK(demultiplexer_2_out0), .RST(RST),
    .Output(n8bitaddrreg_1_output));
  _8bitAddrReg u_8bitaddrreg_2 (
    .Input(demultiplexer_1_out1), .Address(Address[2:0]), .CLK(demultiplexer_2_out1), .RST(RST),
    .Output(n8bitaddrreg_2_output));
  _8bitAddrReg u_8bitaddrreg_3 (
    .Input(demultiplexer_1_out2), .Address(Address[2:0]), .CLK(demultiplexer_2_out2), .RST(RST),
    .Output(n8bitaddrreg_3_output));
  _8bitAddrReg u_8bitaddrreg_4 (
    .Input(demultiplexer_1_out3), .Address(Address[2:0]), .CLK(demultiplexer_2_out3), .RST(RST),
    .Output(n8bitaddrreg_4_output));
  _8bitAddrReg u_8bitaddrreg_5 (
    .Input(demultiplexer_1_out4), .Address(Address[2:0]), .CLK(demultiplexer_2_out4), .RST(RST),
    .Output(n8bitaddrreg_5_output));
  _8bitAddrReg u_8bitaddrreg_6 (
    .Input(demultiplexer_1_out5), .Address(Address[2:0]), .CLK(demultiplexer_2_out5), .RST(RST),
    .Output(n8bitaddrreg_6_output));
  _8bitAddrReg u_8bitaddrreg_7 (
    .Input(demultiplexer_1_out6), .Address(Address[2:0]), .CLK(demultiplexer_2_out6), .RST(RST),
    .Output(n8bitaddrreg_7_output));
  _8bitAddrReg u_8bitaddrreg_8 (
    .Input(demultiplexer_1_out7), .Address(Address[2:0]), .CLK(demultiplexer_2_out7), .RST(RST),
    .Output(n8bitaddrreg_8_output));
  Demultiplexer #(.select(3), .enable("false")) demultiplexer_2 (
    .out0(demultiplexer_2_out0), .out1(demultiplexer_2_out1), .out2(demultiplexer_2_out2),
    .out3(demultiplexer_2_out3), .out4(demultiplexer_2_out4), .out5(demultiplexer_2_out5),
    .out6(demultiplexer_2_out6), .out7(demultiplexer_2_out7), .in(CLK), .sel(Address[5:3]));
  Multiplexer #(.select(3), .width(8), .enable("false")) multiplexer_1 (
    .in0(n8bitaddrreg_1_output), .in1(n8bitaddrreg_2_output), .in2(n8bitaddrreg_3_output),
    .in3(n8bitaddrreg_4_output), .in4(n8bitaddrreg_5_output), .in5(n8bitaddrreg_6_output),
    .in6(n8bitaddrreg_7_output), .in7(n8bitaddrreg_8_output), .out(multiplexer_1_out), .sel(Address[5:3]));
  BitSelector bitselector_1 (.in(multiplexer_1_out), .out(Output), .sel(not_1_out));
  assign not_1_out = ~Address[2:0];  // NOT_Gate not_1, 3 bits wide
endmodule
