// Logisim project 64x64 LED.circ as structural Verilog: 1 circuit, main circuit 64x64 LED Control
module _64x64_LED_Control (
  input  [2:0] in_1,
  input  input_Clock,
  input  [11:0] Initial_Position,
  input  isGame,
  input  [6:0] Keyboard_input,
  input  FINISHED,
  input  CLK,
  input  RST,
  input  [31:0] in_9,
  input  [31:0] in_10,
  input  [31:0] in_11,
  input  [31:0] in_12,
  input  [31:0] in_13,
  input  [31:0] in_14,
  input  [31:0] in_15,
  input  [31:0] in_16,
  output [31:0] out_17,
  output [31:0] out_18,
  output [31:0] out_19,
  output [31:0] out_20,
  output [31:0] out_21,
  output [31:0] out_22,
  output [31:0] out_23,
  output [31:0] out_24,
  output [31:0] out_25,
  output [31:0] out_26,
  output [31:0] out_27,
  output [31:0] out_28,
  output [31:0] out_29,
  output [31:0] out_30,
  output [31:0] out_31,
  output [31:0] out_32,
  output [31:0] out_33,
  output [31:0] out_34,
  output [31:0] out_35,
  output [31:0] out_36,
  output [31:0] out_37,
  output [31:0] out_38,
  output [31:0] out_39,
  output [31:0] out_40,
  output [31:0] out_41,
  output [31:0] out_42,
  output [31:0] out_43,
  output [31:0] out_44,
  output [31:0] out_45,
  output [31:0] out_46,
  output [31:0] out_47,
  output [31:0] out_48,
  output [31:0] out_49,
  output [31:0] out_50,
  output [31:0] out_51,
  output [31:0] out_52,
  output [31:0] out_53,
  output [31:0] out_54,
  output [31:0] out_55,
  output [31:0] out_56,
  output [31:0] out_57,
  output [31:0] out_58,
  output [31:0] out_59,
  output [31:0] out_60,
  output [31:0] out_61,
  output [31:0] out_62,
  output [31:0] out_63,
  output [31:0] out_64,
  output [31:0] out_65,
  output [31:0] out_66,
  output [31:0] out_67,
  output [31:0] out_68,
  output [31:0] out_69,
  output [31:0] out_70,
  output [31:0] out_71,
  output [31:0] out_72,
  output [31:0] out_73,
  output [31:0] out_74,
  output [31:0] out_75,
  output [31:0] out_76,
  output [31:0] out_77,
  output [31:0] out_78,
  output [31:0] out_79,
  output [31:0] out_80,
  output [31:0] out_81,
  output [31:0] out_82,
  output [31:0] out_83,
  output [31:0] out_84,
  output [31:0] out_85,
  output [31:0] out_86,
  output [31:0] out_87,
  output [31:0] out_88,
  output [31:0] out_89,
  output [31:0] out_90,
  output [31:0] out_91,
  output [31:0] out_92,
  output [31:0] out_93,
  output [31:0] out_94,
  output [31:0] out_95,
  output [31:0] out_96,
  output [31:0] out_97,
  output [31:0] out_98,
  output [31:0] out_99,
  output [31:0] out_100,
  output [31:0] out_101,
  output [31:0] out_102,
  output [31:0] out_103,
  output [31:0] out_104,
  output [31:0] out_105,
  output [31:0] out_106,
  output [31:0] out_107,
  output [31:0] out_108,
  output [31:0] out_109,
  output [31:0] out_110,
  output [31:0] out_111,
  output [31:0] out_112,
  output [31:0] out_113,
  output [31:0] out_114,
  output [31:0] out_115,
  output [31:0] out_116,
  output [31:0] out_117,
  output [31:0] out_118,
  output [31:0] out_119,
  output [31:0] out_120,
  output [31:0] out_121,
  output [31:0] out_122,
  output [31:0] out_123,
  output [31:0] out_124,
  output [31:0] out_125,
  output [31:0] out_126,
  output [31:0] out_127,
  output [31:0] out_128,
  output [31:0] out_129,
  output [31:0] out_130,
  output [31:0] out_131,
  output [31:0] out_132,
  output [31:0] out_133,
  output [31:0] out_134,
  output [31:0] out_135,
  output [31:0] out_136,
  output [31:0] out_137,
  output [31:0] out_138,
  output [31:0] out_139,
  output [31:0] out_140,
  output [31:0] out_141,
  output [31:0] out_142,
  output [31:0] out_143,
  output [31:0] out_144
);

  wire and_1_out, and_2_out, isBlocked, movement_check_1_overflow_flag, not_1_out, not_2_out, not_3_out,
       not_4_out, or_129_out, Spawn_Occupied;
  wire [2:0] Direction_input;
  wire [6:0] register_1_q;
  wire [11:0] Current_location, multiplexer_1_out, multiplexer_2_out, New_location;
  wire [31:0] _0r1, _0r2, _0r3, _0r4, _0r5, _0r6, _0r7, _0r8, _0r9, _0r10, _0r11, _0r12, _0r13, _0r14, _0r15,
       _0r16, _0r17, _0r18, _0r19, _0r20, _0r21, _0r22, _0r23, _0r24, _0r25, _0r26, _0r27, _0r28, _0r29,
       _0r30, _0r31, _0r32, _0r33, _0r34, _0r35, _0r36, _0r37, _0r38, _0r39, _0r40, _0r41, _0r42, _0r43,
       _0r44, _0r45, _0r46, _0r47, _0r48, _0r49, _0r50, _0r51, _0r52, _0r53, _0r54, _0r55, _0r56, _0r57,
       _0r58, _0r59, _0r60, _0r61, _0r62, _0r63, _0r64, _1r1, _1r2, _1r3, _1r4, _1r5, _1r6, _1r7, _1r8, _1r9,
       _1r10, _1r11, _1r12, _1r13, _1r14, _1r15, _1r16, _1r17, _1r18, _1r19, _1r20, _1r21, _1r22, _1r23,
       _1r24, _1r25, _1r26, _1r27, _1r28, _1r29, _1r30, _1r31, _1r32, _1r33, _1r34, _1r35, _1r36, _1r37,
       _1r38, _1r39, _1r40, _1r41, _1r42, _1r43, _1r44, _1r45, _1r46, _1r47, _1r48, _1r49, _1r50, _1r51,
       _1r52, _1r53, _1r54, _1r55, _1r56, _1r57, _1r58, _1r59, _1r60, _1r61, _1r62, _1r63, _1r64, minus_0r1,
       minus_0r2, minus_0r3, minus_0r4, minus_0r5, minus_0r6, minus_0r7, minus_0r8, minus_0r9, minus_0r10,
       minus_0r11, minus_0r12, minus_0r13, minus_0r14, minus_0r15, minus_0r16, minus_0r17, minus_0r18,
       minus_0r19, minus_0r20, minus_0r21, minus_0r22, minus_0r23, minus_0r24, minus_0r25, minus_0r26,
       minus_0r27, minus_0r28, minus_0r29, minus_0r30, minus_0r31, minus_0r32, minus_0r33, minus_0r34,
       minus_0r35, minus_0r36, minus_0r37, minus_0r38, minus_0r39, minus_0r40, minus_0r41, minus_0r42,
       minus_0r43, minus_0r44, minus_0r45, minus_0r46, minus_0r47, minus_0r48, minus_0r49, minus_0r50,
       minus_0r51, minus_0r52, minus_0r53, minus_0r54, minus_0r55, minus_0r56, minus_0r57, minus_0r58,
       minus_0r59, minus_0r60, minus_0r61, minus_0r62, minus_0r63, minus_0r64, minus_1r1, minus_1r2,
       minus_1r3, minus_1r4, minus_1r5, minus_1r6, minus_1r7, minus_1r8, minus_1r9, minus_1r10, minus_1r11,
       minus_1r12, minus_1r13, minus_1r14, minus_1r15, minus_1r16, minus_1r17, minus_1r18, minus_1r19,
       minus_1r20, minus_1r21, minus_1r22, minus_1r23, minus_1r24, minus_1r25, minus_1r26, minus_1r27,
       minus_1r28, minus_1r29, minus_1r30, minus_1r31, minus_1r32, minus_1r33, minus_1r34, minus_1r35,
       minus_1r36, minus_1r37, minus_1r38, minus_1r39, minus_1r40, minus_1r41, minus_1r42, minus_1r43,
       minus_1r44, minus_1r45, minus_1r46, minus_1r47, minus_1r48, minus_1r49, minus_1r50, minus_1r51,
       minus_1r52, minus_1r53, minus_1r54, minus_1r55, minus_1r56, minus_1r57, minus_1r58, minus_1r59,
       minus_1r60, minus_1r61, minus_1r62, minus_1r63, minus_1r64;

  _8x64_LED_Control u_8x64_led_control_1 (
    .in_2(in_16), .CLK(CLK), .RST(RST), .out_14(_1r1), .out_16(_1r2), .out_18(_1r3), .out_20(_1r4),
    .out_22(_1r5), .out_24(_1r6), .out_26(_1r7), .out_28(_1r8), .out_15(_0r1), .out_17(_0r2), .out_19(_0r3),
    .out_21(_0r4), .out_23(_0r5), .out_25(_0r6), .out_27(_0r7), .out_29(_0r8), .in_12(in_1), .in_13(1'b1));  // open: in_11, in_8, in_7, in_6, in_5, in_4, in_3, in_1
  _8x64_LED_Control u_8x64_led_control_2 (
    .in_2(in_15), .CLK(CLK), .RST(RST), .out_14(_1r9), .out_16(_1r10), .out_18(_1r11), .out_20(_1r12),
    .out_22(_1r13), .out_24(_1r14), .out_26(_1r15), .out_28(_1r16), .out_15(_0r9), .out_17(_0r10),
    .out_19(_0r11), .out_21(_0r12), .out_23(_0r13), .out_25(_0r14), .out_27(_0r15), .out_29(_0r16),
    .in_12(in_1), .in_13(1'b1));  // open: in_11, in_8, in_7, in_6, in_5, in_4, in_3, in_1
  _8x64_LED_Control u_8x64_led_control_3 (
    .in_2(in_14), .CLK(CLK), .RST(RST), .out_14(_1r17), .out_16(_1r18), .out_18(_1r19), .out_20(_1r20),
    .out_22(_1r21), .out_24(_1r22), .out_26(_1r23), .out_28(_1r24), .out_15(_0r17), .out_17(_0r18),
    .out_19(_0r19), .out_21(_0r20), .out_23(_0r21), .out_25(_0r22), .out_27(_0r23), .out_29(_0r24),
    .in_12(in_1), .in_13(1'b1));  // open: in_11, in_8, in_7, in_6, in_5, in_4, in_3, in_1
  _8x64_LED_Control u_8x64_led_control_4 (
    .in_2(in_13), .CLK(CLK), .RST(RST), .out_14(_1r25), .out_16(_1r26), .out_18(_1r27), .out_20(_1r28),
    .out_22(_1r29), .out_24(_1r30), .out_26(_1r31), .out_28(_1r32), .out_15(_0r25), .out_17(_0r26),
    .out_19(_0r27), .out_21(_0r28), .out_23(_0r29), .out_25(_0r30), .out_27(_0r31), .out_29(_0r32),
    .in_12(in_1), .in_13(1'b1));  // open: in_11, in_8, in_7, in_6, in_5, in_4, in_3, in_1
  _8x64_LED_Control u_8x64_led_control_5 (
    .in_2(in_12), .CLK(CLK), .RST(RST), .out_14(_1r33), .out_16(_1r34), .out_18(_1r35), .out_20(_1r36),
    .out_22(_1r37), .out_24(_1r38), .out_26(_1r39), .out_28(_1r40), .out_15(_0r33), .out_17(_0r34),
    .out_19(_0r35), .out_21(_0r36), .out_23(_0r37), .out_25(_0r38), .out_27(_0r39), .out_29(_0r40),
    .in_12(in_1), .in_13(1'b1));  // open: in_11, in_8, in_7, in_6, in_5, in_4, in_3, in_1
  _8x64_LED_Control u_8x64_led_control_6 (
    .in_2(in_11), .CLK(CLK), .RST(RST), .out_14(_1r41), .out_16(_1r42), .out_18(_1r43), .out_20(_1r44),
    .out_22(_1r45), .out_24(_1r46), .out_26(_1r47), .out_28(_1r48), .out_15(_0r41), .out_17(_0r42),
    .out_19(_0r43), .out_21(_0r44), .out_23(_0r45), .out_25(_0r46), .out_27(_0r47), .out_29(_0r48),
    .in_12(in_1), .in_13(1'b1));  // open: in_11, in_8, in_7, in_6, in_5, in_4, in_3, in_1
  _8x64_LED_Control u_8x64_led_control_7 (
    .in_2(in_10), .CLK(CLK), .RST(RST), .out_14(_1r49), .out_16(_1r50), .out_18(_1r51), .out_20(_1r52),
    .out_22(_1r53), .out_24(_1r54), .out_26(_1r55), .out_28(_1r56), .out_15(_0r49), .out_17(_0r50),
    .out_19(_0r51), .out_21(_0r52), .out_23(_0r53), .out_25(_0r54), .out_27(_0r55), .out_29(_0r56),
    .in_12(in_1), .in_13(1'b1));  // open: in_11, in_8, in_7, in_6, in_5, in_4, in_3, in_1
  _8x64_LED_Control u_8x64_led_control_8 (
    .in_2(in_9), .CLK(CLK), .RST(RST), .out_14(_1r57), .out_16(_1r58), .out_18(_1r59), .out_20(_1r60),
    .out_22(_1r61), .out_24(_1r62), .out_26(_1r63), .out_28(_1r64), .out_15(_0r57), .out_17(_0r58),
    .out_19(_0r59), .out_21(_0r60), .out_23(_0r61), .out_25(_0r62), .out_27(_0r63), .out_29(_0r64),
    .in_12(in_1), .in_13(1'b1));  // open: in_11, in_8, in_7, in_6, in_5, in_4, in_3, in_1
  assign out_65 = minus_0r25 | _0r25;  // OR_Gate or_1, 32 bits wide
  assign out_66 = minus_0r26 | _0r26;  // OR_Gate or_2, 32 bits wide
  assign out_81 = minus_0r33 | _0r33;  // OR_Gate or_3, 32 bits wide
  assign out_82 = minus_0r34 | _0r34;  // OR_Gate or_4, 32 bits wide
  assign out_97 = minus_0r41 | _0r41;  // OR_Gate or_5, 32 bits wide
  assign out_98 = minus_0r42 | _0r42;  // OR_Gate or_6, 32 bits wide
  assign out_113 = minus_0r49 | _0r49;  // OR_Gate or_7, 32 bits wide
  assign out_114 = minus_0r50 | _0r50;  // OR_Gate or_8, 32 bits wide
  assign out_129 = minus_0r57 | _0r57;  // OR_Gate or_9, 32 bits wide
  assign out_17 = _0r1 | minus_0r1;  // OR_Gate or_10, 32 bits wide
  assign out_67 = minus_0r27 | _0r27;  // OR_Gate or_11, 32 bits wide
  assign out_83 = minus_0r35 | _0r35;  // OR_Gate or_12, 32 bits wide
  assign out_99 = minus_0r43 | _0r43;  // OR_Gate or_13, 32 bits wide
  assign out_115 = minus_0r51 | _0r51;  // OR_Gate or_14, 32 bits wide
  assign out_130 = minus_0r58 | _0r58;  // OR_Gate or_15, 32 bits wide
  assign out_131 = minus_0r59 | _0r59;  // OR_Gate or_16, 32 bits wide
  assign out_18 = _0r2 | minus_0r2;  // OR_Gate or_17, 32 bits wide
  assign out_33 = minus_0r9 | _0r9;  // OR_Gate or_18, 32 bits wide
  assign out_34 = minus_0r10 | _0r10;  // OR_Gate or_19, 32 bits wide
  assign out_35 = minus_0r11 | _0r11;  // OR_Gate or_20, 32 bits wide
  assign out_36 = minus_0r12 | _0r12;  // OR_Gate or_21, 32 bits wide
  assign out_37 = minus_0r13 | _0r13;  // OR_Gate or_22, 32 bits wide
  assign out_49 = minus_0r17 | _0r17;  // OR_Gate or_23, 32 bits wide
  assign out_50 = minus_0r18 | _0r18;  // OR_Gate or_24, 32 bits wide
  assign out_68 = minus_0r28 | _0r28;  // OR_Gate or_25, 32 bits wide
  assign out_69 = minus_0r29 | _0r29;  // OR_Gate or_26, 32 bits wide
  assign out_84 = minus_0r36 | _0r36;  // OR_Gate or_27, 32 bits wide
  assign out_100 = minus_0r44 | _0r44;  // OR_Gate or_28, 32 bits wide
  assign out_116 = minus_0r52 | _0r52;  // OR_Gate or_29, 32 bits wide
  assign out_132 = minus_0r60 | _0r60;  // OR_Gate or_30, 32 bits wide
  assign out_19 = _0r3 | minus_0r3;  // OR_Gate or_31, 32 bits wide
  assign out_38 = minus_0r14 | _0r14;  // OR_Gate or_32, 32 bits wide
  assign out_39 = minus_0r15 | _0r15;  // OR_Gate or_33, 32 bits wide
  assign out_40 = minus_0r16 | _0r16;  // OR_Gate or_34, 32 bits wide
  assign out_51 = minus_0r19 | _0r19;  // OR_Gate or_35, 32 bits wide
  assign out_52 = minus_0r20 | _0r20;  // OR_Gate or_36, 32 bits wide
  assign out_70 = minus_0r30 | _0r30;  // OR_Gate or_37, 32 bits wide
  assign out_101 = minus_0r45 | _0r45;  // OR_Gate or_38, 32 bits wide
  assign out_133 = minus_0r61 | _0r61;  // OR_Gate or_39, 32 bits wide
  assign out_20 = _0r4 | minus_0r4;  // OR_Gate or_40, 32 bits wide
  assign out_53 = minus_0r21 | _0r21;  // OR_Gate or_41, 32 bits wide
  assign out_85 = minus_0r37 | _0r37;  // OR_Gate or_42, 32 bits wide
  assign out_86 = minus_0r38 | _0r38;  // OR_Gate or_43, 32 bits wide
  assign out_117 = minus_0r53 | _0r53;  // OR_Gate or_44, 32 bits wide
  assign out_134 = minus_0r62 | _0r62;  // OR_Gate or_45, 32 bits wide
  assign out_21 = _0r5 | minus_0r5;  // OR_Gate or_46, 32 bits wide
  assign out_54 = minus_0r22 | _0r22;  // OR_Gate or_47, 32 bits wide
  assign out_71 = minus_0r31 | _0r31;  // OR_Gate or_48, 32 bits wide
  assign out_87 = minus_0r39 | _0r39;  // OR_Gate or_49, 32 bits wide
  assign out_102 = minus_0r46 | _0r46;  // OR_Gate or_50, 32 bits wide
  assign out_118 = minus_0r54 | _0r54;  // OR_Gate or_51, 32 bits wide
  assign out_135 = minus_0r63 | _0r63;  // OR_Gate or_52, 32 bits wide
  assign out_22 = _0r6 | minus_0r6;  // OR_Gate or_53, 32 bits wide
  assign out_55 = minus_0r23 | _0r23;  // OR_Gate or_54, 32 bits wide
  assign out_72 = minus_0r32 | _0r32;  // OR_Gate or_55, 32 bits wide
  assign out_103 = minus_0r47 | _0r47;  // OR_Gate or_56, 32 bits wide
  assign out_119 = minus_0r55 | _0r55;  // OR_Gate or_57, 32 bits wide
  assign out_23 = _0r7 | minus_0r7;  // OR_Gate or_58, 32 bits wide
  assign out_56 = minus_0r24 | _0r24;  // OR_Gate or_59, 32 bits wide
  assign out_73 = minus_1r25 | _1r25;  // OR_Gate or_60, 32 bits wide
  assign out_88 = minus_0r40 | _0r40;  // OR_Gate or_61, 32 bits wide
  assign out_104 = minus_0r48 | _0r48;  // OR_Gate or_62, 32 bits wide
  assign out_120 = minus_0r56 | _0r56;  // OR_Gate or_63, 32 bits wide
  assign out_136 = minus_0r64 | _0r64;  // OR_Gate or_64, 32 bits wide
  assign out_24 = _0r8 | minus_0r8;  // OR_Gate or_65, 32 bits wide
  assign out_41 = minus_1r9 | _1r9;  // OR_Gate or_66, 32 bits wide
  assign out_57 = minus_1r17 | _1r17;  // OR_Gate or_67, 32 bits wide
  assign out_74 = minus_1r26 | _1r26;  // OR_Gate or_68, 32 bits wide
  assign out_89 = minus_1r33 | _1r33;  // OR_Gate or_69, 32 bits wide
  assign out_105 = minus_1r41 | _1r41;  // OR_Gate or_70, 32 bits wide
  assign out_121 = minus_1r49 | _1r49;  // OR_Gate or_71, 32 bits wide
  assign out_137 = minus_1r57 | _1r57;  // OR_Gate or_72, 32 bits wide
  assign out_25 = _1r1 | minus_1r1;  // OR_Gate or_73, 32 bits wide
  assign out_42 = minus_1r10 | _1r10;  // OR_Gate or_74, 32 bits wide
  assign out_43 = minus_1r11 | _1r11;  // OR_Gate or_75, 32 bits wide
  assign out_58 = minus_1r18 | _1r18;  // OR_Gate or_76, 32 bits wide
  assign out_75 = minus_1r27 | _1r27;  // OR_Gate or_77, 32 bits wide
  assign out_76 = minus_1r28 | _1r28;  // OR_Gate or_78, 32 bits wide
  assign out_90 = minus_1r34 | _1r34;  // OR_Gate or_79, 32 bits wide
  assign out_91 = minus_1r35 | _1r35;  // OR_Gate or_80, 32 bits wide
  assign out_106 = minus_1r42 | _1r42;  // OR_Gate or_81, 32 bits wide
  assign out_122 = minus_1r50 | _1r50;  // OR_Gate or_82, 32 bits wide
  assign out_138 = minus_1r58 | _1r58;  // OR_Gate or_83, 32 bits wide
  assign out_26 = _1r2 | minus_1r2;  // OR_Gate or_84, 32 bits wide
  assign out_44 = minus_1r12 | _1r12;  // OR_Gate or_85, 32 bits wide
  assign out_59 = minus_1r19 | _1r19;  // OR_Gate or_86, 32 bits wide
  assign out_77 = minus_1r29 | _1r29;  // OR_Gate or_87, 32 bits wide
  assign out_107 = minus_1r43 | _1r43;  // OR_Gate or_88, 32 bits wide
  assign out_123 = minus_1r51 | _1r51;  // OR_Gate or_89, 32 bits wide
  assign out_139 = minus_1r59 | _1r59;  // OR_Gate or_90, 32 bits wide
  assign out_27 = _1r3 | minus_1r3;  // OR_Gate or_91, 32 bits wide
  assign out_45 = minus_1r13 | _1r13;  // OR_Gate or_92, 32 bits wide
  assign out_46 = minus_1r14 | _1r14;  // OR_Gate or_93, 32 bits wide
  assign out_60 = minus_1r20 | _1r20;  // OR_Gate or_94, 32 bits wide
  assign out_92 = minus_1r36 | _1r36;  // OR_Gate or_95, 32 bits wide
  assign out_108 = minus_1r44 | _1r44;  // OR_Gate or_96, 32 bits wide
  assign out_124 = minus_1r52 | _1r52;  // OR_Gate or_97, 32 bits wide
  assign out_140 = minus_1r60 | _1r60;  // OR_Gate or_98, 32 bits wide
  assign out_28 = _1r4 | minus_1r4;  // OR_Gate or_99, 32 bits wide
  assign out_47 = minus_1r15 | _1r15;  // OR_Gate or_100, 32 bits wide
  assign out_48 = minus_1r16 | _1r16;  // OR_Gate or_101, 32 bits wide
  assign out_61 = minus_1r21 | _1r21;  // OR_Gate or_102, 32 bits wide
  assign out_78 = minus_1r30 | _1r30;  // OR_Gate or_103, 32 bits wide
  assign out_93 = minus_1r37 | _1r37;  // OR_Gate or_104, 32 bits wide
  assign out_109 = minus_1r45 | _1r45;  // OR_Gate or_105, 32 bits wide
  assign out_125 = minus_1r53 | _1r53;  // OR_Gate or_106, 32 bits wide
  assign out_141 = minus_1r61 | _1r61;  // OR_Gate or_107, 32 bits wide
  assign out_79 = minus_1r31 | _1r31;  // OR_Gate or_108, 32 bits wide
  assign out_94 = minus_1r38 | _1r38;  // OR_Gate or_109, 32 bits wide
  assign out_110 = minus_1r46 | _1r46;  // OR_Gate or_110, 32 bits wide
  assign out_126 = minus_1r54 | _1r54;  // OR_Gate or_111, 32 bits wide
  assign out_142 = minus_1r62 | _1r62;  // OR_Gate or_112, 32 bits wide
  assign out_29 = _1r5 | minus_1r5;  // OR_Gate or_113, 32 bits wide
  assign out_62 = minus_1r22 | _1r22;  // OR_Gate or_114, 32 bits wide
  assign out_63 = minus_1r23 | _1r23;  // OR_Gate or_115, 32 bits wide
  assign out_80 = minus_1r32 | _1r32;  // OR_Gate or_116, 32 bits wide
  assign out_95 = minus_1r39 | _1r39;  // OR_Gate or_117, 32 bits wide
  assign out_96 = minus_1r40 | _1r40;  // OR_Gate or_118, 32 bits wide
  assign out_127 = minus_1r55 | _1r55;  // OR_Gate or_119, 32 bits wide
  assign out_128 = minus_1r56 | _1r56;  // OR_Gate or_120, 32 bits wide
  assign out_143 = minus_1r63 | _1r63;  // OR_Gate or_121, 32 bits wide
  assign out_30 = _1r6 | minus_1r6;  // OR_Gate or_122, 32 bits wide
  assign out_64 = minus_1r24 | _1r24;  // OR_Gate or_123, 32 bits wide
  assign out_111 = minus_1r47 | _1r47;  // OR_Gate or_124, 32 bits wide
  assign out_112 = minus_1r48 | _1r48;  // OR_Gate or_125, 32 bits wide
  assign out_144 = minus_1r64 | _1r64;  // OR_Gate or_126, 32 bits wide
  assign out_31 = _1r7 | minus_1r7;  // OR_Gate or_127, 32 bits wide
  assign out_32 = _1r8 | minus_1r8;  // OR_Gate or_128, 32 bits wide
  Multiplexer #(.width(12)) multiplexer_1 (
    .in0(Initial_Position), .in1(12'h43), .out(multiplexer_1_out), .sel(Spawn_Occupied));  // open: en
  Register #(.width(7)) register_1 (.D(Keyboard_input), .Q(register_1_q), .clk(input_Clock));  // open: en, clr
  _12_bit_selector u_12_bit_selector_1 (
    .Select(Initial_Position), .in_10(_0r1), .in_26(_0r2), .in_42(_0r3), .in_58(_0r4), .in_74(_0r5),
    .in_90(_0r6), .in_106(_0r7), .in_122(_0r8), .in_11(_1r1), .in_27(_1r2), .in_43(_1r3), .in_59(_1r4),
    .in_75(_1r5), .in_91(_1r6), .in_107(_1r7), .in_123(_1r8), .Probed_bit(Spawn_Occupied), .in_12(_0r9),
    .in_28(_0r10), .in_44(_0r11), .in_60(_0r12), .in_76(_0r13), .in_92(_0r14), .in_108(_0r15),
    .in_124(_0r16), .in_13(_1r9), .in_29(_1r10), .in_45(_1r11), .in_61(_1r12), .in_77(_1r13), .in_93(_1r14),
    .in_109(_1r15), .in_125(_1r16), .in_14(_0r17), .in_30(_0r18), .in_46(_0r19), .in_62(_0r20),
    .in_78(_0r21), .in_94(_0r22), .in_110(_0r23), .in_126(_0r24), .in_15(_1r17), .in_31(_1r18),
    .in_47(_1r19), .in_63(_1r20), .in_79(_1r21), .in_95(_1r22), .in_111(_1r23), .in_127(_1r24),
    .in_16(_0r25), .in_32(_0r26), .in_48(_0r27), .in_64(_0r28), .in_80(_0r29), .in_96(_0r30), .in_112(_0r31),
    .in_128(_0r32), .in_17(_1r25), .in_33(_1r26), .in_49(_1r27), .in_65(_1r28), .in_81(_1r29), .in_97(_1r30),
    .in_113(_1r31), .in_129(_1r32), .in_2(_0r33), .in_3(_1r33), .in_4(_0r41), .in_5(_1r41), .in_6(_0r49),
    .in_7(_1r49), .in_8(_0r57), .in_9(_1r57), .in_18(_0r34), .in_19(_1r34), .in_20(_0r42), .in_21(_1r42),
    .in_22(_0r50), .in_23(_1r50), .in_24(_0r58), .in_25(_1r58), .in_34(_0r35), .in_35(_1r35), .in_36(_0r43),
    .in_37(_1r43), .in_38(_0r51), .in_39(_1r51), .in_40(_0r59), .in_41(_1r59), .in_50(_0r36), .in_51(_1r36),
    .in_52(_0r44), .in_53(_1r44), .in_54(_0r52), .in_55(_1r52), .in_56(_0r60), .in_57(_1r60), .in_66(_0r37),
    .in_67(_1r37), .in_68(_0r45), .in_69(_1r45), .in_70(_0r53), .in_71(_1r53), .in_72(_0r61), .in_73(_1r61),
    .in_82(_0r38), .in_83(_1r38), .in_84(_0r46), .in_85(_1r46), .in_86(_0r54), .in_87(_1r54), .in_88(_0r62),
    .in_89(_1r62), .in_98(_0r39), .in_99(_1r39), .in_100(_0r47), .in_101(_1r47), .in_102(_0r55),
    .in_103(_1r55), .in_104(_0r63), .in_105(_1r63), .in_114(_0r40), .in_115(_1r40), .in_116(_0r48),
    .in_117(_1r48), .in_118(_0r56), .in_119(_1r56), .in_120(_0r64), .in_121(_1r64));
  movement_check movement_check_1 (
    .New_location(New_location), .Overflow_flag(movement_check_1_overflow_flag),
    .Current_position(multiplexer_2_out), .Movement_direction(Direction_input));
  Multiplexer #(.width(12)) multiplexer_2 (
    .in0(Current_location), .in1(multiplexer_1_out), .out(multiplexer_2_out), .sel(not_1_out));  // open: en
  not not_1 (not_1_out, isGame);
  ROM #(.addrWidth(7), .dataWidth(3)) rom_1 (.addr(register_1_q), .data(Direction_input));  // open: sel
  or or_129 (or_129_out, movement_check_1_overflow_flag, isBlocked);
  not not_2 (not_2_out, input_Clock);
  _12_bit_selector u_12_bit_selector_2 (
    .Select(New_location), .in_10(_0r1), .in_26(_0r2), .in_42(_0r3), .in_58(_0r4), .in_74(_0r5),
    .in_90(_0r6), .in_106(_0r7), .in_122(_0r8), .in_11(_1r1), .in_27(_1r2), .in_43(_1r3), .in_59(_1r4),
    .in_75(_1r5), .in_91(_1r6), .in_107(_1r7), .in_123(_1r8), .Probed_bit(isBlocked), .in_12(_0r9),
    .in_28(_0r10), .in_44(_0r11), .in_60(_0r12), .in_76(_0r13), .in_92(_0r14), .in_108(_0r15),
    .in_124(_0r16), .in_13(_1r9), .in_29(_1r10), .in_45(_1r11), .in_61(_1r12), .in_77(_1r13), .in_93(_1r14),
    .in_109(_1r15), .in_125(_1r16), .in_14(_0r17), .in_30(_0r18), .in_46(_0r19), .in_62(_0r20),
    .in_78(_0r21), .in_94(_0r22), .in_110(_0r23), .in_126(_0r24), .in_15(_1r17), .in_31(_1r18),
    .in_47(_1r19), .in_63(_1r20), .in_79(_1r21), .in_95(_1r22), .in_111(_1r23), .in_127(_1r24),
    .in_16(_0r25), .in_32(_0r26), .in_48(_0r27), .in_64(_0r28), .in_80(_0r29), .in_96(_0r30), .in_112(_0r31),
    .in_128(_0r32), .in_17(_1r25), .in_33(_1r26), .in_49(_1r27), .in_65(_1r28), .in_81(_1r29), .in_97(_1r30),
    .in_113(_1r31), .in_129(_1r32), .in_2(_0r33), .in_3(_1r33), .in_4(_0r41), .in_5(_1r41), .in_6(_0r49),
    .in_7(_1r49), .in_8(_0r57), .in_9(_1r57), .in_18(_0r34), .in_19(_1r34), .in_20(_0r42), .in_21(_1r42),
    .in_22(_0r50), .in_23(_1r50), .in_24(_0r58), .in_25(_1r58), .in_34(_0r35), .in_35(_1r35), .in_36(_0r43),
    .in_37(_1r43), .in_38(_0r51), .in_39(_1r51), .in_40(_0r59), .in_41(_1r59), .in_50(_0r36), .in_51(_1r36),
    .in_52(_0r44), .in_53(_1r44), .in_54(_0r52), .in_55(_1r52), .in_56(_0r60), .in_57(_1r60), .in_66(_0r37),
    .in_67(_1r37), .in_68(_0r45), .in_69(_1r45), .in_70(_0r53), .in_71(_1r53), .in_72(_0r61), .in_73(_1r61),
    .in_82(_0r38), .in_83(_1r38), .in_84(_0r46), .in_85(_1r46), .in_86(_0r54), .in_87(_1r54), .in_88(_0r62),
    .in_89(_1r62), .in_98(_0r39), .in_99(_1r39), .in_100(_0r47), .in_101(_1r47), .in_102(_0r55),
    .in_103(_1r55), .in_104(_0r63), .in_105(_1r63), .in_114(_0r40), .in_115(_1r40), .in_116(_0r48),
    .in_117(_1r48), .in_118(_0r56), .in_119(_1r56), .in_120(_0r64), .in_121(_1r64));
  screen_map screen_map_1 (
    .Select(Current_location), .out_11(minus_0r1), .out_27(minus_0r2), .out_43(minus_0r3),
    .out_59(minus_0r4), .out_75(minus_0r5), .out_91(minus_0r6), .out_107(minus_0r7), .out_123(minus_0r8),
    .out_12(minus_1r1), .out_28(minus_1r2), .out_44(minus_1r3), .out_60(minus_1r4), .out_76(minus_1r5),
    .out_92(minus_1r6), .out_108(minus_1r7), .out_124(minus_1r8), .out_13(minus_0r9), .out_29(minus_0r10),
    .out_45(minus_0r11), .out_61(minus_0r12), .out_77(minus_0r13), .out_93(minus_0r14), .out_109(minus_0r15),
    .out_125(minus_0r16), .out_14(minus_1r9), .out_30(minus_1r10), .out_46(minus_1r11), .out_62(minus_1r12),
    .out_78(minus_1r13), .out_94(minus_1r14), .out_110(minus_1r15), .out_126(minus_1r16),
    .out_15(minus_0r17), .out_31(minus_0r18), .out_47(minus_0r19), .out_63(minus_0r20), .out_79(minus_0r21),
    .out_95(minus_0r22), .out_111(minus_0r23), .out_127(minus_0r24), .out_16(minus_1r17),
    .out_32(minus_1r18), .out_48(minus_1r19), .out_64(minus_1r20), .out_80(minus_1r21), .out_96(minus_1r22),
    .out_112(minus_1r23), .out_128(minus_1r24), .out_17(minus_0r25), .out_33(minus_0r26),
    .out_49(minus_0r27), .out_65(minus_0r28), .out_81(minus_0r29), .out_97(minus_0r30), .out_113(minus_0r31),
    .out_129(minus_0r32), .out_18(minus_1r25), .out_34(minus_1r26), .out_50(minus_1r27), .out_66(minus_1r28),
    .out_82(minus_1r29), .out_98(minus_1r30), .out_114(minus_1r31), .out_130(minus_1r32), .out_3(minus_0r33),
    .out_19(minus_0r34), .out_35(minus_0r35), .out_51(minus_0r36), .out_67(minus_0r37), .out_83(minus_0r38),
    .out_99(minus_0r39), .out_115(minus_0r40), .out_4(minus_1r33), .out_20(minus_1r34), .out_36(minus_1r35),
    .out_52(minus_1r36), .out_68(minus_1r37), .out_84(minus_1r38), .out_100(minus_1r39),
    .out_116(minus_1r40), .out_5(minus_0r41), .out_21(minus_0r42), .out_37(minus_0r43), .out_53(minus_0r44),
    .out_69(minus_0r45), .out_85(minus_0r46), .out_101(minus_0r47), .out_117(minus_0r48), .out_6(minus_1r41),
    .out_22(minus_1r42), .out_38(minus_1r43), .out_54(minus_1r44), .out_70(minus_1r45), .out_86(minus_1r46),
    .out_102(minus_1r47), .out_118(minus_1r48), .out_7(minus_0r49), .out_23(minus_0r50), .out_39(minus_0r51),
    .out_55(minus_0r52), .out_71(minus_0r53), .out_87(minus_0r54), .out_103(minus_0r55),
    .out_119(minus_0r56), .out_8(minus_1r49), .out_24(minus_1r50), .out_40(minus_1r51), .out_56(minus_1r52),
    .out_72(minus_1r53), .out_88(minus_1r54), .out_104(minus_1r55), .out_120(minus_1r56), .out_9(minus_0r57),
    .out_25(minus_0r58), .out_41(minus_0r59), .out_57(minus_0r60), .out_73(minus_0r61), .out_89(minus_0r62),
    .out_105(minus_0r63), .out_121(minus_0r64), .out_10(minus_1r57), .out_26(minus_1r58),
    .out_42(minus_1r59), .out_58(minus_1r60), .out_74(minus_1r61), .out_90(minus_1r62), .out_106(minus_1r63),
    .out_122(minus_1r64), .in_1(and_1_out));
  and and_1 (and_1_out, FINISHED, CLK);
  not not_3 (not_3_out, or_129_out);
  Register #(.width(12), .trigger("falling")) register_2 (
    .D(New_location), .Q(Current_location), .clk(not_4_out));  // open: en, clr
  not not_4 (not_4_out, and_2_out);
  and and_2 (and_2_out, not_3_out, not_2_out);

  // Other names for the same wires on the sheet: Spawn[11:0] = Initial_Position; vis_clk = CLK

  // Notes on the sheet:
  //   contents of rom_1 (hex, n*v repeats v):
  //   97*0 7 0 0 5 14*0 6 0 0 0 4
endmodule
