// Logisim project 8bitAddrReg.circ as structural Verilog: 1 circuit, main circuit 8bitAddrReg
module _8bitAddrReg (
  input  [7:0] Input,
  input  [2:0] Address,
  input  CLK,
  input  RST,
  output [7:0] Output
);

  wire demultiplexer_1_out0, demultiplexer_1_out1, demultiplexer_1_out2, demultiplexer_1_out3,
       demultiplexer_1_out4, demultiplexer_1_out5, demultiplexer_1_out6, demultiplexer_1_out7;

  Demultiplexer #(.select(3), .enable("false")) demultiplexer_1 (
    .out0(demultiplexer_1_out0), .out1(demultiplexer_1_out1), .out2(demultiplexer_1_out2),
    .out3(demultiplexer_1_out3), .out4(demultiplexer_1_out4), .out5(demultiplexer_1_out5),
    .out6(demultiplexer_1_out6), .out7(demultiplexer_1_out7), .in(CLK), .sel(Address));
  D_Flip_Flop d_ff_1 (.clk(demultiplexer_1_out0), .D(Input[7]), .Q(Output[7]), .reset(RST));  // open: Qn, preset, en
  D_Flip_Flop d_ff_2 (.clk(demultiplexer_1_out1), .D(Input[6]), .Q(Output[6]), .reset(RST));  // open: Qn, preset, en
  D_Flip_Flop d_ff_3 (.clk(demultiplexer_1_out2), .D(Input[5]), .Q(Output[5]), .reset(RST));  // open: Qn, preset, en
  D_Flip_Flop d_ff_4 (.clk(demultiplexer_1_out3), .D(Input[4]), .Q(Output[4]), .reset(RST));  // open: Qn, preset, en
  D_Flip_Flop d_ff_5 (.clk(demultiplexer_1_out4), .D(Input[3]), .Q(Output[3]), .reset(RST));  // open: Qn, preset, en
  D_Flip_Flop d_ff_6 (.clk(demultiplexer_1_out5), .D(Input[2]), .Q(Output[2]), .reset(RST));  // open: Qn, preset, en
  D_Flip_Flop d_ff_7 (.clk(demultiplexer_1_out6), .D(Input[1]), .Q(Output[1]), .reset(RST));  // open: Qn, preset, en
  D_Flip_Flop d_ff_8 (.clk(demultiplexer_1_out7), .D(Input[0]), .Q(Output[0]), .reset(RST));  // open: Qn, preset, en
endmodule
