// Logisim project 8x32bitRegister.circ as structural Verilog: 1 circuit, main circuit 8x32bit Register
module _8x32bit_Register (
  input  [31:0] Inputs,
  input  [31:0] in_2,
  input  [31:0] in_3,
  input  [31:0] in_4,
  input  [31:0] in_5,
  input  [31:0] in_6,
  input  [31:0] in_7,
  input  [31:0] in_8,
  input  CLK,
  input  RST,
  input  [2:0] Select,
  output [31:0] out_12,
  output [31:0] out_13,
  output [31:0] out_14,
  output [31:0] out_15,
  output [31:0] out_16,
  output [31:0] out_17,
  output [31:0] out_18,
  output [31:0] out_19
);

  wire demultiplexer_1_out0, demultiplexer_1_out1, demultiplexer_1_out2, demultiplexer_1_out3,
       demultiplexer_1_out4, demultiplexer_1_out5, demultiplexer_1_out6, demultiplexer_1_out7;

  Demultiplexer #(.select(3), .enable("false")) demultiplexer_1 (
    .out0(demultiplexer_1_out0), .out1(demultiplexer_1_out1), .out2(demultiplexer_1_out2),
    .out3(demultiplexer_1_out3), .out4(demultiplexer_1_out4), .out5(demultiplexer_1_out5),
    .out6(demultiplexer_1_out6), .out7(demultiplexer_1_out7), .in(CLK), .sel(Select));
  Register #(.width(32)) register_1 (.D(Inputs), .Q(out_12), .clk(demultiplexer_1_out0), .clr(RST));  // open: en
  Register #(.width(32)) register_2 (.D(in_2), .Q(out_13), .clk(demultiplexer_1_out1), .clr(RST));  // open: en
  Register #(.width(32)) register_3 (.D(in_3), .Q(out_14), .clk(demultiplexer_1_out2), .clr(RST));  // open: en
  Register #(.width(32)) register_4 (.D(in_4), .Q(out_15), .clk(demultiplexer_1_out3), .clr(RST));  // open: en
  Register #(.width(32)) register_5 (.D(in_5), .Q(out_16), .clk(demultiplexer_1_out4), .clr(RST));  // open: en
  Register #(.width(32)) register_6 (.D(in_6), .Q(out_17), .clk(demultiplexer_1_out5), .clr(RST));  // open: en
  Register #(.width(32)) register_7 (.D(in_7), .Q(out_18), .clk(demultiplexer_1_out6), .clr(RST));  // open: en
  Register #(.width(32)) register_8 (.D(in_8), .Q(out_19), .clk(demultiplexer_1_out7), .clr(RST));  // open: en

  // Notes on the sheet:
  //   Outputs
endmodule
