// Logisim project 8x64 LED.circ as structural Verilog: 1 circuit, main circuit 8x64 LED Control
module _8x64_LED_Control (
  input  [2:0] in_1,
  input  [31:0] in_2,
  input  [2:0] in_3,
  input  [2:0] in_4,
  input  [2:0] in_5,
  input  [2:0] in_6,
  input  [2:0] in_7,
  input  [2:0] in_8,
  input  CLK,
  input  RST,
  input  [2:0] in_11,
  input  [2:0] in_12,
  input  in_13,
  output [31:0] out_14,
  output [31:0] out_15,
  output [31:0] out_16,
  output [31:0] out_17,
  output [31:0] out_18,
  output [31:0] out_19,
  output [31:0] out_20,
  output [31:0] out_21,
  output [31:0] out_22,
  output [31:0] out_23,
  output [31:0] out_24,
  output [31:0] out_25,
  output [31:0] out_26,
  output [31:0] out_27,
  output [31:0] out_28,
  output [31:0] out_29
);

  wire [2:0] multiplexer_1_out, multiplexer_2_out, multiplexer_3_out, multiplexer_4_out, multiplexer_5_out,
       multiplexer_6_out, multiplexer_7_out, multiplexer_8_out;

  Multiplexer #(.width(3)) multiplexer_1 (.in0(in_1), .in1(in_12), .out(multiplexer_1_out), .sel(in_13));  // open: en
  Multiplexer #(.width(3)) multiplexer_2 (.in0(in_3), .in1(in_12), .out(multiplexer_2_out), .sel(in_13));  // open: en
  Multiplexer #(.width(3)) multiplexer_3 (.in0(in_4), .in1(in_12), .out(multiplexer_3_out), .sel(in_13));  // open: en
  Multiplexer #(.width(3)) multiplexer_4 (.in0(in_5), .in1(in_12), .out(multiplexer_4_out), .sel(in_13));  // open: en
  Multiplexer #(.width(3)) multiplexer_5 (.in0(in_6), .in1(in_12), .out(multiplexer_5_out), .sel(in_13));  // open: en
  Multiplexer #(.width(3)) multiplexer_6 (.in0(in_7), .in1(in_12), .out(multiplexer_6_out), .sel(in_13));  // open: en
  Multiplexer #(.width(3)) multiplexer_7 (.in0(in_8), .in1(in_12), .out(multiplexer_7_out), .sel(in_13));  // open: en
  Multiplexer #(.width(3)) multiplexer_8 (.in0(in_11), .in1(in_12), .out(multiplexer_8_out), .sel(in_13));  // open: en
  LED_Control_8x8 led_control_8x8_1 (
    .SEL(in_2[3:0]), .CLK(CLK), .RST(RST), .out_12(out_28[7:0]), .out_11(out_26[7:0]), .out_10(out_24[7:0]),
    .out_9(out_22[7:0]), .out_8(out_20[7:0]), .out_7(out_18[7:0]), .out_6(out_16[7:0]), .out_5(out_14[7:0]),
    .in_1(multiplexer_1_out));
  LED_Control_8x8 led_control_8x8_2 (
    .SEL(in_2[7:4]), .CLK(CLK), .RST(RST), .out_12(out_28[15:8]), .out_11(out_26[15:8]),
    .out_10(out_24[15:8]), .out_9(out_22[15:8]), .out_8(out_20[15:8]), .out_7(out_18[15:8]),
    .out_6(out_16[15:8]), .out_5(out_14[15:8]), .in_1(multiplexer_2_out));
  LED_Control_8x8 led_control_8x8_3 (
    .SEL(in_2[11:8]), .CLK(CLK), .RST(RST), .out_12(out_28[23:16]), .out_11(out_26[23:16]),
    .out_10(out_24[23:16]), .out_9(out_22[23:16]), .out_8(out_20[23:16]), .out_7(out_18[23:16]),
    .out_6(out_16[23:16]), .out_5(out_14[23:16]), .in_1(multiplexer_3_out));
  LED_Control_8x8 led_control_8x8_4 (
    .SEL(in_2[15:12]), .CLK(CLK), .RST(RST), .out_12(out_28[31:24]), .out_11(out_26[31:24]),
    .out_10(out_24[31:24]), .out_9(out_22[31:24]), .out_8(out_20[31:24]), .out_7(out_18[31:24]),
    .out_6(out_16[31:24]), .out_5(out_14[31:24]), .in_1(multiplexer_4_out));
  LED_Control_8x8 led_control_8x8_5 (
    .SEL(in_2[19:16]), .CLK(CLK), .RST(RST), .out_12(out_29[7:0]), .out_11(out_27[7:0]),
    .out_10(out_25[7:0]), .out_9(out_23[7:0]), .out_8(out_21[7:0]), .out_7(out_19[7:0]), .out_6(out_17[7:0]),
    .out_5(out_15[7:0]), .in_1(multiplexer_5_out));
  LED_Control_8x8 led_control_8x8_6 (
    .SEL(in_2[23:20]), .CLK(CLK), .RST(RST), .out_12(out_29[15:8]), .out_11(out_27[15:8]),
    .out_10(out_25[15:8]), .out_9(out_23[15:8]), .out_8(out_21[15:8]), .out_7(out_19[15:8]),
    .out_6(out_17[15:8]), .out_5(out_15[15:8]), .in_1(multiplexer_6_out));
  LED_Control_8x8 led_control_8x8_7 (
    .SEL(in_2[27:24]), .CLK(CLK), .RST(RST), .out_12(out_29[23:16]), .out_11(out_27[23:16]),
    .out_10(out_25[23:16]), .out_9(out_23[23:16]), .out_8(out_21[23:16]), .out_7(out_19[23:16]),
    .out_6(out_17[23:16]), .out_5(out_15[23:16]), .in_1(multiplexer_7_out));
  LED_Control_8x8 led_control_8x8_8 (
    .SEL(in_2[31:28]), .CLK(CLK), .RST(RST), .out_12(out_29[31:24]), .out_11(out_27[31:24]),
    .out_10(out_25[31:24]), .out_9(out_23[31:24]), .out_8(out_21[31:24]), .out_7(out_19[31:24]),
    .out_6(out_17[31:24]), .out_5(out_15[31:24]), .in_1(multiplexer_8_out));
endmodule
