// Logisim project 8x8 LED.circ as structural Verilog: 1 circuit, main circuit LED Control 8x8
module LED_Control_8x8 (
  input  [2:0] in_1,
  input  [3:0] SEL,
  input  CLK,
  input  RST,
  output [7:0] out_5,
  output [7:0] out_6,
  output [7:0] out_7,
  output [7:0] out_8,
  output [7:0] out_9,
  output [7:0] out_10,
  output [7:0] out_11,
  output [7:0] out_12
);

  wire d_ff_1_q, d_ff_1_qn;
  wire [2:0] counter_1_q;
  wire [7:0] demultiplexer_1_out0, demultiplexer_1_out1, demultiplexer_1_out2, demultiplexer_1_out3,
       demultiplexer_1_out4, demultiplexer_1_out5, demultiplexer_1_out6, demultiplexer_1_out7,
       multiplexer_1_out, rom_1_data, rom_2_data, rom_3_data, rom_4_data, rom_5_data;

  D_Flip_Flop #(.trigger("falling")) d_ff_1 (
    .clk(CLK), .D(d_ff_1_qn), .Q(d_ff_1_q), .Qn(d_ff_1_qn), .reset(RST));  // open: preset, en
  Counter #(.width(3), .max('h7)) counter_1 (
    .Q(counter_1_q), .clk(d_ff_1_q), .clr(RST));  // open: load, D, count, carry
  ROM #(.addrWidth(7)) rom_1 (.addr({SEL, counter_1_q}), .data(rom_1_data));  // open: sel
  ROM #(.addrWidth(7)) rom_2 (.addr({SEL, counter_1_q}), .data(rom_2_data));  // open: sel
  ROM #(.addrWidth(7)) rom_3 (.addr({SEL, counter_1_q}), .data(rom_3_data));  // open: sel
  ROM #(.addrWidth(7)) rom_4 (.addr({SEL, counter_1_q}), .data(rom_4_data));  // open: sel
  ROM #(.addrWidth(7)) rom_5 (.addr({SEL, counter_1_q}), .data(rom_5_data));  // open: sel
  Demultiplexer #(.select(3), .width(8), .enable("false")) demultiplexer_1 (
    .out0(demultiplexer_1_out0), .out1(demultiplexer_1_out1), .out2(demultiplexer_1_out2),
    .out3(demultiplexer_1_out3), .out4(demultiplexer_1_out4), .out5(demultiplexer_1_out5),
    .out6(demultiplexer_1_out6), .out7(demultiplexer_1_out7), .in(multiplexer_1_out), .sel(counter_1_q));
  Multiplexer #(.select(3), .width(8)) multiplexer_1 (
    .in0(rom_5_data), .in1(rom_4_data), .in2(rom_3_data), .in3(rom_2_data), .in4(rom_1_data),
    .out(multiplexer_1_out), .sel(in_1));  // open: in5, in6, in7, en
  _8x8bit_Register u_8x8bit_register_1 (
    .in_1(demultiplexer_1_out0), .in_2(demultiplexer_1_out1), .in_3(demultiplexer_1_out2),
    .in_4(demultiplexer_1_out3), .in_5(demultiplexer_1_out4), .in_6(demultiplexer_1_out5), .CLK(CLK),
    .RST(RST), .Select(counter_1_q), .in_7(demultiplexer_1_out6), .in_8(demultiplexer_1_out7),
    .Outputs(out_5), .out_13(out_6), .out_14(out_7), .out_15(out_8), .out_16(out_9), .out_17(out_10),
    .out_18(out_11), .out_19(out_12));

  // Notes on the sheet:
  //   contents of rom_1 (hex, n*v repeats v):
  //   9*ff 81 bd 31 31 bd 81 ff ff 81 bd 81 81 bd 81 e7 ff 81 bd 31 31 bd 81 e7 ff 81 bd 8c 8c bd 81 ff ff
  //   81 bd 3c 3c bd 81 ff ff 81 bd 8c 8c bd 81 e7 ff 81 bd 3c 3c bd 81 e7 e7 81 bd 81 81 bd 81 ff e7 81
  //   bd 31 31 bd 81 ff e7 81 bd 81 81 bd 81 e7 e7 81 bd 31 31 bd 81 e7 e7 81 bd 8c 8c bd 81 ff e7 81 bd
  //   3c 3c bd 81 ff e7 81 bd 8c 8c bd 81 e7 e7 81 bd 3c 3c bd 81 e7
  //   contents of rom_2 (hex, n*v repeats v):
  //   9*ff 81 81 11 11 81 81 ff ff 6*81 e7 ff 81 81 11 11 81 81 e7 ff 81 81 88 88 81 81 ff ff 81 81 18 18
  //   81 81 ff ff 81 81 88 88 81 81 e7 ff 81 81 18 18 81 81 e7 e7 6*81 ff e7 81 81 11 11 81 81 ff e7 6*81
  //   e7 e7 81 81 11 11 81 81 e7 e7 81 81 88 88 81 81 ff e7 81 81 18 18 81 81 ff e7 81 81 88 88 81 81 e7
  //   e7 81 81 18 18 81 81 e7
  //   contents of rom_3 (hex, n*v repeats v):
  //   9*ff e7 e7 1 1 e7 e7 ff ff e7 e7 81 81 e7 e7 e7 ff e7 e7 1 1 e7 e7 e7 ff e7 e7 80 80 e7 e7 ff ff e7
  //   e7 0 0 e7 e7 ff ff e7 e7 80 80 e7 e7 e7 ff e7 e7 0 0 6*e7 81 81 e7 e7 ff e7 e7 e7 1 1 e7 e7 ff e7 e7
  //   e7 81 81 6*e7 1 1 6*e7 80 80 e7 e7 ff e7 e7 e7 0 0 e7 e7 ff e7 e7 e7 80 80 6*e7 0 0 e7 e7 e7
  //   contents of rom_4 (hex, n*v repeats v):
  //   9*ff c3 81 1 1 81 c3 ff ff c3 4*81 c3 e7 ff c3 81 1 1 81 c3 e7 ff c3 81 80 80 81 c3 ff ff c3 81 0 0
  //   81 c3 ff ff c3 81 80 80 81 c3 e7 ff c3 81 0 0 81 c3 e7 e7 c3 4*81 c3 ff e7 c3 81 1 1 81 c3 ff e7 c3
  //   4*81 c3 e7 e7 c3 81 1 1 81 c3 e7 e7 c3 81 80 80 81 c3 ff e7 c3 81 0 0 81 c3 ff e7 c3 81 80 80 81 c3
  //   e7 e7 c3 81 0 0 81 c3 e7
  //   contents of rom_5 (hex, n*v repeats v):
  //   9*ff 81 81 1 1 81 81 ff ff 6*81 e7 ff 81 81 1 1 81 81 e7 ff 81 81 80 80 81 81 ff ff 81 81 0 0 81 81
  //   ff ff 81 81 80 80 81 81 e7 ff 81 81 0 0 81 81 e7 e7 6*81 ff e7 81 81 1 1 81 81 ff e7 6*81 e7 e7 81
  //   81 1 1 81 81 e7 e7 81 81 80 80 81 81 ff e7 81 81 0 0 81 81 ff e7 81 81 80 80 81 81 e7 e7 81 81 0 0
  //   81 81 e7
  //   LED 8x8
endmodule
