// Logisim project Algorithm.circ as structural Verilog: 1 circuit, main circuit main
module main (
  input  [7:0] Room_Limit,
  input  [3:0] RAM_Read_Data,
  input  CLK,
  input  START,
  output [5:0] Safe_Room,
  output [5:0] RAM_Address,
  output [3:0] RAM_Data,
  output RAM_Write,
  output RAM_CLK,
  output Ram_Clear,
  output Running,
  output Finished
);

  wire Address_Register_CLK, Address_Register_RST, and_1_out, and_3_out, and_4_out, and_5_out, and_7_out,
       bitselector_1_out, comparator_2_eq, comparator_3_eq, comparator_5_eq, comparator_6_gt, Counter_RST,
       CURRENT, Door_REG_CLK, Door_REG_RST, Flag, Init, Next_Iteration, not_1_out, or_7_out, or_8_out, POP,
       PUSH, Queue_CLK, RAM_REG_CLK, RAM_REG_RST, RAND_CLK, Repeat, Room_Limit_Flag,
       Room_occupance_RAM_output, Room_RAM_CLK, Room_RAM_RST;
  wire [1:0] DIRECTION, not_2_out;
  wire [3:0] doorchooser_1_choosen_rooms, doordatagenerator_1_doors__inversed, doordatagenerator_2_doors,
       n4bitaddrreg_1_output, or_9_out, or_10_out, register_2_q;
  wire [5:0] Address_Register_Value, addressdirection_1_address_of_room_in_direction, main_1_output,
       multiplexer_1_out, multiplexer_2_out;
  wire [7:0] Program_Counter, Queue_Size, Room_Count;
  wire [13:3] rom_1_data;

  ROM #(.dataWidth(18)) rom_1 (
    .addr(Program_Counter),
    .data({POP, PUSH, Queue_CLK, Address_Register_CLK, rom_1_data[13], RAND_CLK, RAM_Write, RAM_CLK, rom_1_data[9], Door_REG_CLK, rom_1_data[7], RAM_REG_CLK, rom_1_data[5], Room_RAM_CLK, rom_1_data[3], DIRECTION, CURRENT}));  // open: sel
  or or_1 (Counter_RST, START, Repeat);
  or or_2 (Address_Register_RST, rom_1_data[13], Counter_RST);
  or or_3 (Ram_Clear, rom_1_data[9], Counter_RST);
  or or_4 (Door_REG_RST, rom_1_data[7], Counter_RST);
  or or_5 (RAM_REG_RST, rom_1_data[5], Counter_RST);
  or or_6 (Room_RAM_RST, rom_1_data[3], Counter_RST);
  Multiplexer #(.width(6), .enable("false")) multiplexer_1 (
    .in0(RAM_Address), .in1(Safe_Room), .out(multiplexer_1_out), .sel(Init));
  FIFO_main main_1 (
    .Input(multiplexer_1_out), .SIZE(Queue_Size), .PUSH(or_7_out), .POP(POP), .RST(Counter_RST),
    .Output(main_1_output), .CLK(Queue_CLK));  // open: FULL, EMPTY
  or or_7 (or_7_out, and_3_out, Init);
  roomLimit_main main_2 (
    .CLK(or_7_out), .Room_Limit_Flag(Room_Limit_Flag), .Room_Limit(Room_Limit), ._0(Counter_RST),
    .Room_Counter(Room_Count));
  D_Flip_Flop d_ff_1 (.clk(START), .D(1'b1), .Q(Running), .reset(and_1_out));  // open: Qn, preset, en
  and and_1 (and_1_out, Finished, Running);
  Comparator #(.mode("unsigned")) comparator_1 (.a(Program_Counter), .b(8'h3), .lt(Init));  // open: gt, eq
  and and_2 (Finished, Room_Limit_Flag, comparator_2_eq);
  Comparator #(.mode("unsigned")) comparator_2 (.a(Program_Counter), .b(8'h3), .eq(comparator_2_eq));  // open: gt, lt
  Comparator comparator_3 (.a(Queue_Size), .b({8{1'b0}}), .eq(comparator_3_eq));  // open: gt, lt
  and and_3 (and_3_out, PUSH, Flag);
  Multiplexer #(.width(6), .enable("false")) multiplexer_2 (
    .in0(main_1_output), .in1(Safe_Room), .out(multiplexer_2_out), .sel(comparator_3_eq));
  Register #(.width(6)) register_1 (
    .D(multiplexer_2_out), .Q(Address_Register_Value), .clk(Address_Register_CLK), .clr(Address_Register_RST));  // open: en
  Random #(.width(6)) random_1 (.clk(or_8_out), .out(Safe_Room));  // open: next, clr
  or or_8 (or_8_out, and_4_out, Repeat);
  and and_4 (and_4_out, START, ~Running);  // AND_Gate
  not not_1 (not_1_out, Next_Iteration);
  and and_5 (and_5_out, CLK, Running, ~Finished);  // AND_Gate
  Counter #(.max('h2d)) counter_1 (
    .load(Next_Iteration), .D(8'h3), .count(not_1_out), .Q(Program_Counter), .clk(and_5_out));  // open: carry, clr
  Comparator comparator_4 (.a(Program_Counter), .b(8'h2d), .eq(Next_Iteration));  // open: gt, lt
  and and_6 (Repeat, comparator_5_eq, comparator_6_gt);
  Comparator #(.mode("unsigned")) comparator_5 (.a(Queue_Size), .b({8{1'b0}}), .eq(comparator_5_eq));  // open: gt, lt
  Comparator #(.mode("unsigned")) comparator_6 (.a(Room_Count), .b(8'h1), .gt(comparator_6_gt));  // open: eq, lt
  addressDirection addressdirection_1 (
    .Direction(DIRECTION), .Address(Address_Register_Value),
    .Address_of_room_in_direction(addressdirection_1_address_of_room_in_direction));
  doorChooser doorchooser_1 (
    .Addr(Address_Register_Value), .CLK(RAND_CLK), .Choosen_Rooms(doorchooser_1_choosen_rooms));
  assign not_2_out = ~DIRECTION;  // NOT_Gate not_2, 2 bits wide
  _64bitAddrReg Room_occupance_RAM (
    .Input(Flag), .RST(Room_RAM_RST), .Address(RAM_Address), .CLK(and_7_out),
    .Output(Room_occupance_RAM_output));
  and and_7 (and_7_out, Flag, Room_RAM_CLK);
  Multiplexer #(.width(6), .enable("false")) multiplexer_3 (
    .in0(addressdirection_1_address_of_room_in_direction), .in1(Address_Register_Value), .out(RAM_Address),
    .sel(CURRENT));
  BitSelector #(.width(4)) bitselector_1 (.in(doorchooser_1_choosen_rooms), .out(bitselector_1_out), .sel(not_2_out));
  and and_8 (Flag, bitselector_1_out, ~Room_Limit_Flag, ~Room_occupance_RAM_output);  // AND_Gate
  doorDataGenerator doordatagenerator_1 (
    .Input(Flag), .Direction(DIRECTION), .Doors__Inversed(doordatagenerator_1_doors__inversed));  // open: Doors
  doorDataGenerator doordatagenerator_2 (
    .Input(Flag), .Direction(DIRECTION), .Doors(doordatagenerator_2_doors));  // open: Doors__Inversed
  Register #(.width(4)) register_2 (
    .D(RAM_Read_Data), .Q(register_2_q), .clk(RAM_REG_CLK), .clr(RAM_REG_RST));  // open: en
  _4BitAddrReg u_4bitaddrreg_1 (
    .Input(doordatagenerator_2_doors), .Address(DIRECTION), .CLK(Door_REG_CLK), ._0(Door_REG_RST),
    .Output(n4bitaddrreg_1_output));
  assign or_9_out = doordatagenerator_1_doors__inversed | register_2_q;  // OR_Gate or_9, 4 bits wide
  assign or_10_out = register_2_q | n4bitaddrreg_1_output;  // OR_Gate or_10, 4 bits wide
  Multiplexer #(.width(4), .enable("false")) multiplexer_4 (
    .in0(or_9_out), .in1(or_10_out), .out(RAM_Data), .sel(CURRENT));

  // Other names for the same wires on the sheet: Queue_RST = Counter_RST; RAM_Reset = Ram_Clear; RST = START;
  //   Starting_Room[5:0] = Safe_Room

  // Notes on the sheet:
  //   INPUT
  //   OUTPUT
  //   Program Control
  //   contents of rom_1 (hex, n*v repeats v):
  //   0 8000 0 20a0 20000 25000 20000 140 10800 18c00 10800 20 10 0 2 142 10802 18c02 10802 22 12 2 4 144
  //   10804 18c04 10804 24 14 4 6 146 10806 18c06 10806 26 16 6 1 41 1 801 c01 20801 28000 20000
  //   Queue
  //   Program Start
  //   Conditions to push onto Queue
  //   Room Counter / Checks for Room Limit
  //   Condition when to initialise / Finishing condition
  //   Program Counter
  //   Set starting room
  //   Current Room Address
  //   Condition to repeat 
  //   Conditions to create a room
  //   Address of Room in current Direction
  //   Generate RAM Data
  //   Door Data read from RAM
  //   Door Data for current Room
  //   Door Data for room in current Directoin
endmodule
