// Logisim project FIFO.circ as structural Verilog: 1 circuit, main circuit main
module main (
  input  [5:0] Input,
  input  PUSH,
  input  RST,
  input  CLK,
  input  POP,
  output FULL,
  output [7:0] SIZE,
  output EMPTY,
  output [5:0] Output
);

  wire and_1_out, and_2_out, comparator_1_eq, comparator_2_eq, not_1_out;
  wire [7:0] adder_1_out, counter_1_q, counter_2_q, multiplexer_1_out;

  and and_1 (and_1_out, PUSH, ~comparator_2_eq);  // AND_Gate
  and and_2 (and_2_out, POP, ~comparator_1_eq);  // AND_Gate
  and and_3 (FULL, comparator_2_eq, PUSH);
  Counter #(.trigger("falling")) counter_1 (
    .count(and_1_out), .Q(counter_1_q), .clk(CLK), .clr(RST));  // open: load, D, carry
  Counter #(.trigger("falling")) counter_2 (
    .count(and_2_out), .Q(counter_2_q), .clk(CLK), .clr(RST));  // open: load, D, carry
  Adder adder_1 (.a(counter_1_q), .b(8'h1), .out(adder_1_out));  // open: cin, cout
  Multiplexer #(.width(8), .enable("false")) multiplexer_1 (
    .in0(counter_1_q), .in1(counter_2_q), .out(multiplexer_1_out), .sel(and_2_out));
  Comparator #(.mode("unsigned")) comparator_1 (
    .a(counter_1_q), .b(counter_2_q), .eq(comparator_1_eq));  // open: gt, lt
  Comparator #(.mode("unsigned")) comparator_2 (
    .a(adder_1_out), .b(counter_2_q), .eq(comparator_2_eq));  // open: gt, lt
  not not_1 (not_1_out, and_1_out);
  Subtractor subtractor_1 (.a(counter_1_q), .b(counter_2_q), .out(SIZE));  // open: bin, bout
  and and_4 (EMPTY, comparator_1_eq, POP);
  assign Output = and_1_out ? Input : 6'bz;  // Controlled_Buffer controlled_buffer_1
  RAM #(.dataWidth(6)) ram_1 (
    .addr(multiplexer_1_out), .data(Output), .sel(1'b1), .clk(CLK), .ld(not_1_out), .clr(RST));
endmodule
