// Logisim project Main.circ as structural Verilog: 4 circuits, main circuit main
module sefe_start_calc (
  input  [5:0] Safe_Room_Address,
  output [11:0] Safe_Pixel_Address
);

  wire [11:0] adder_1_out, multiplier_1_out, multiplier_2_out;

  Multiplier #(.width(12)) multiplier_1 (
    .a({{9{1'b0}}, Safe_Room_Address[2:0]}), .b(12'h8), .out(multiplier_1_out));  // open: cin, cout
  Multiplier #(.width(12)) multiplier_2 (
    .a({{9{1'b0}}, Safe_Room_Address[5:3]}), .b(12'h200), .out(multiplier_2_out));  // open: cin, cout
  Adder #(.width(12)) adder_1 (.a(12'h43), .b(multiplier_1_out), .out(adder_1_out));  // open: cin, cout
  Adder #(.width(12)) adder_2 (.a(adder_1_out), .b(multiplier_2_out), .out(Safe_Pixel_Address));  // open: cin, cout
endmodule

module main (
  input  in_1,
  input  in_2
);

  wire Algorithm_Finished, Algorithm_Init, Algorithm_Running, and_1_out, CLK, D_out, L_out, Manual_Write_CLK,
       minus_1_2_out, minus_1_3_out, minus_1_out, minus_10_out, plus_1_2_out, plus_1_3_out, plus_1_out,
       plus_10_out, R_out, Reset, Room_Design, roomdatainterface_1_bottom_door_choosen,
       roomdatainterface_1_left_door_choosen, roomdatainterface_1_right_door_choosen,
       roomdatainterface_1_top_door_choosen, U_out;
  wire [2:0] main_2_out_2;
  wire [3:0] Manual_Data;
  wire [5:0] Manual_Address, SAFE;
  wire [6:0] key_out;
  wire [7:0] main_1_out_6, main_1_out_7, main_1_out_8, main_1_out_9, main_1_out_10, main_1_out_11,
       main_1_out_12, main_1_room_select_display_output, Room_Limit;
  wire [11:0] sefe_start_calc_1_safe_pixel_address;
  wire [15:0] roomlimitinterface_1__7_segment_output;
  wire [31:0] n64x64_led_control_1_out_17, n64x64_led_control_1_out_18, n64x64_led_control_1_out_19,
       n64x64_led_control_1_out_20, n64x64_led_control_1_out_21, n64x64_led_control_1_out_22,
       n64x64_led_control_1_out_23, n64x64_led_control_1_out_24, n64x64_led_control_1_out_25,
       n64x64_led_control_1_out_26, n64x64_led_control_1_out_27, n64x64_led_control_1_out_28,
       n64x64_led_control_1_out_29, n64x64_led_control_1_out_30, n64x64_led_control_1_out_31,
       n64x64_led_control_1_out_32, n64x64_led_control_1_out_33, n64x64_led_control_1_out_34,
       n64x64_led_control_1_out_35, n64x64_led_control_1_out_36, n64x64_led_control_1_out_37,
       n64x64_led_control_1_out_38, n64x64_led_control_1_out_39, n64x64_led_control_1_out_40,
       n64x64_led_control_1_out_41, n64x64_led_control_1_out_42, n64x64_led_control_1_out_43,
       n64x64_led_control_1_out_44, n64x64_led_control_1_out_45, n64x64_led_control_1_out_46,
       n64x64_led_control_1_out_47, n64x64_led_control_1_out_48, n64x64_led_control_1_out_49,
       n64x64_led_control_1_out_50, n64x64_led_control_1_out_51, n64x64_led_control_1_out_52,
       n64x64_led_control_1_out_53, n64x64_led_control_1_out_54, n64x64_led_control_1_out_55,
       n64x64_led_control_1_out_56, n64x64_led_control_1_out_57, n64x64_led_control_1_out_58,
       n64x64_led_control_1_out_59, n64x64_led_control_1_out_60, n64x64_led_control_1_out_61,
       n64x64_led_control_1_out_62, n64x64_led_control_1_out_63, n64x64_led_control_1_out_64,
       n64x64_led_control_1_out_65, n64x64_led_control_1_out_66, n64x64_led_control_1_out_67,
       n64x64_led_control_1_out_68, n64x64_led_control_1_out_69, n64x64_led_control_1_out_70,
       n64x64_led_control_1_out_71, n64x64_led_control_1_out_72, n64x64_led_control_1_out_73,
       n64x64_led_control_1_out_74, n64x64_led_control_1_out_75, n64x64_led_control_1_out_76,
       n64x64_led_control_1_out_77, n64x64_led_control_1_out_78, n64x64_led_control_1_out_79,
       n64x64_led_control_1_out_80, n64x64_led_control_1_out_81, n64x64_led_control_1_out_82,
       n64x64_led_control_1_out_83, n64x64_led_control_1_out_84, n64x64_led_control_1_out_85,
       n64x64_led_control_1_out_86, n64x64_led_control_1_out_87, n64x64_led_control_1_out_88,
       n64x64_led_control_1_out_89, n64x64_led_control_1_out_90, n64x64_led_control_1_out_91,
       n64x64_led_control_1_out_92, n64x64_led_control_1_out_93, n64x64_led_control_1_out_94,
       n64x64_led_control_1_out_95, n64x64_led_control_1_out_96, n64x64_led_control_1_out_97,
       n64x64_led_control_1_out_98, n64x64_led_control_1_out_99, n64x64_led_control_1_out_100,
       n64x64_led_control_1_out_101, n64x64_led_control_1_out_102, n64x64_led_control_1_out_103,
       n64x64_led_control_1_out_104, n64x64_led_control_1_out_105, n64x64_led_control_1_out_106,
       n64x64_led_control_1_out_107, n64x64_led_control_1_out_108, n64x64_led_control_1_out_109,
       n64x64_led_control_1_out_110, n64x64_led_control_1_out_111, n64x64_led_control_1_out_112,
       n64x64_led_control_1_out_113, n64x64_led_control_1_out_114, n64x64_led_control_1_out_115,
       n64x64_led_control_1_out_116, n64x64_led_control_1_out_117, n64x64_led_control_1_out_118,
       n64x64_led_control_1_out_119, n64x64_led_control_1_out_120, n64x64_led_control_1_out_121,
       n64x64_led_control_1_out_122, n64x64_led_control_1_out_123, n64x64_led_control_1_out_124,
       n64x64_led_control_1_out_125, n64x64_led_control_1_out_126, n64x64_led_control_1_out_127,
       n64x64_led_control_1_out_128, n64x64_led_control_1_out_129, n64x64_led_control_1_out_130,
       n64x64_led_control_1_out_131, n64x64_led_control_1_out_132, n64x64_led_control_1_out_133,
       n64x64_led_control_1_out_134, n64x64_led_control_1_out_135, n64x64_led_control_1_out_136,
       n64x64_led_control_1_out_137, n64x64_led_control_1_out_138, n64x64_led_control_1_out_139,
       n64x64_led_control_1_out_140, n64x64_led_control_1_out_141, n64x64_led_control_1_out_142,
       n64x64_led_control_1_out_143, n64x64_led_control_1_out_144, program_1_out_9, program_1_out_10,
       program_1_out_11, program_1_out_12, program_1_out_13, program_1_out_14, program_1_out_16,
       program_1_out_19;

  Button button_1 (.out(Algorithm_Init));
  LED led_1 (.in(Algorithm_Running));
  LED led_2 (.in(Algorithm_Finished));
  Button plus_10 (.out(plus_10_out));
  Button plus_1 (.out(plus_1_out));
  roomLimitInterface roomlimitinterface_1 (
    ._7_Segment_Output(roomlimitinterface_1__7_segment_output), .plus_10(plus_10_out), .plus_1(plus_1_out),
    .minus_10(minus_10_out), .minus_1(minus_1_out), .Data_Output(Room_Limit));
  Button minus_10 (.out(minus_10_out));
  Button minus_1 (.out(minus_1_out));
  Button button_2 (.out(Reset));
  Button button_3 (.out(Room_Design));
  _7_Segment_Display u_7_segment_display_1 (
    .g(roomlimitinterface_1__7_segment_output[15]), .f(roomlimitinterface_1__7_segment_output[14]),
    .a(roomlimitinterface_1__7_segment_output[13]), .b(roomlimitinterface_1__7_segment_output[12]),
    .e(roomlimitinterface_1__7_segment_output[11]), .d(roomlimitinterface_1__7_segment_output[10]),
    .c(roomlimitinterface_1__7_segment_output[9]), .dp(roomlimitinterface_1__7_segment_output[8]));
  Clock clock_1 (.out(CLK));
  _7_Segment_Display u_7_segment_display_2 (
    .g(roomlimitinterface_1__7_segment_output[7]), .f(roomlimitinterface_1__7_segment_output[6]),
    .a(roomlimitinterface_1__7_segment_output[5]), .b(roomlimitinterface_1__7_segment_output[4]),
    .e(roomlimitinterface_1__7_segment_output[3]), .d(roomlimitinterface_1__7_segment_output[2]),
    .c(roomlimitinterface_1__7_segment_output[1]), .dp(roomlimitinterface_1__7_segment_output[0]));
  DotMatrix #(.inputtype("row"), .matrixcols(32), .matrixrows(32)) dotmatrix_1 (
    .row0(n64x64_led_control_1_out_17), .row1(n64x64_led_control_1_out_18),
    .row2(n64x64_led_control_1_out_19), .row3(n64x64_led_control_1_out_20),
    .row4(n64x64_led_control_1_out_21), .row5(n64x64_led_control_1_out_22),
    .row6(n64x64_led_control_1_out_23), .row7(n64x64_led_control_1_out_24),
    .row8(n64x64_led_control_1_out_33), .row9(n64x64_led_control_1_out_34),
    .row10(n64x64_led_control_1_out_35), .row11(n64x64_led_control_1_out_36),
    .row12(n64x64_led_control_1_out_37), .row13(n64x64_led_control_1_out_38),
    .row14(n64x64_led_control_1_out_39), .row15(n64x64_led_control_1_out_40),
    .row16(n64x64_led_control_1_out_49), .row17(n64x64_led_control_1_out_50),
    .row18(n64x64_led_control_1_out_51), .row19(n64x64_led_control_1_out_52),
    .row20(n64x64_led_control_1_out_53), .row21(n64x64_led_control_1_out_54),
    .row22(n64x64_led_control_1_out_55), .row23(n64x64_led_control_1_out_56),
    .row24(n64x64_led_control_1_out_65), .row25(n64x64_led_control_1_out_66),
    .row26(n64x64_led_control_1_out_67), .row27(n64x64_led_control_1_out_68),
    .row28(n64x64_led_control_1_out_69), .row29(n64x64_led_control_1_out_70),
    .row30(n64x64_led_control_1_out_71), .row31(n64x64_led_control_1_out_72));
  DotMatrix #(.inputtype("row"), .matrixcols(32), .matrixrows(32)) dotmatrix_2 (
    .row0(n64x64_led_control_1_out_81), .row1(n64x64_led_control_1_out_82),
    .row2(n64x64_led_control_1_out_83), .row3(n64x64_led_control_1_out_84),
    .row4(n64x64_led_control_1_out_85), .row5(n64x64_led_control_1_out_86),
    .row6(n64x64_led_control_1_out_87), .row7(n64x64_led_control_1_out_88),
    .row8(n64x64_led_control_1_out_97), .row9(n64x64_led_control_1_out_98),
    .row10(n64x64_led_control_1_out_99), .row11(n64x64_led_control_1_out_100),
    .row12(n64x64_led_control_1_out_101), .row13(n64x64_led_control_1_out_102),
    .row14(n64x64_led_control_1_out_103), .row15(n64x64_led_control_1_out_104),
    .row16(n64x64_led_control_1_out_113), .row17(n64x64_led_control_1_out_114),
    .row18(n64x64_led_control_1_out_115), .row19(n64x64_led_control_1_out_116),
    .row20(n64x64_led_control_1_out_117), .row21(n64x64_led_control_1_out_118),
    .row22(n64x64_led_control_1_out_119), .row23(n64x64_led_control_1_out_120),
    .row24(n64x64_led_control_1_out_129), .row25(n64x64_led_control_1_out_130),
    .row26(n64x64_led_control_1_out_131), .row27(n64x64_led_control_1_out_132),
    .row28(n64x64_led_control_1_out_133), .row29(n64x64_led_control_1_out_134),
    .row30(n64x64_led_control_1_out_135), .row31(n64x64_led_control_1_out_136));
  Program program_1 (
    .Manual_Write(in_1), .Manual_Write_CLK(Manual_Write_CLK), .Manual_Data(Manual_Data),
    .Manual_Address(Manual_Address), .Algorithm_Init(Algorithm_Init), .Room_Limit(Room_Limit), .CLK(CLK),
    .RAM_Manual_RST(Reset), .out_9(program_1_out_9), .out_10(program_1_out_10), .out_11(program_1_out_11),
    .out_12(program_1_out_12), .out_13(program_1_out_13), .out_14(program_1_out_14),
    .out_15(Algorithm_Running), .out_17(Algorithm_Finished), .out_16(program_1_out_16), .out_18(SAFE),
    .out_19(program_1_out_19));
  Button plus_1_2 (.out(plus_1_2_out));
  Button minus_1_2 (.out(minus_1_2_out));
  Button plus_1_3 (.out(plus_1_3_out));
  Button minus_1_3 (.out(minus_1_3_out));
  Button U (.out(U_out));
  Button L (.out(L_out));
  Button D (.out(D_out));
  Button button_4 (.out(Manual_Write_CLK));
  sefe_start_calc sefe_start_calc_1 (
    .Safe_Room_Address(SAFE), .Safe_Pixel_Address(sefe_start_calc_1_safe_pixel_address));
  roomAddressInterface_main main_1 (
    .Row_minus_minus(minus_1_2_out), .Row_plus_plus(plus_1_2_out), .Column_minus_minus(minus_1_3_out),
    .Column_plus_plus(plus_1_3_out), .Room_Select_Display_Output(main_1_room_select_display_output),
    .out_6(main_1_out_6), .out_7(main_1_out_7), .out_8(main_1_out_8), .out_9(main_1_out_9),
    .out_10(main_1_out_10), .out_11(main_1_out_11), .out_12(main_1_out_12), .Room_Address(Manual_Address));
  Button R (.out(R_out));
  DotMatrix #(.inputtype("row"), .matrixcols(8), .matrixrows(8)) dotmatrix_3 (
    .row0(main_1_room_select_display_output), .row1(main_1_out_6), .row2(main_1_out_7), .row3(main_1_out_8),
    .row4(main_1_out_9), .row5(main_1_out_10), .row6(main_1_out_11), .row7(main_1_out_12));
  roomDataInterface roomdatainterface_1 (
    .Top_Door_Switch(U_out), .Right_Door_Switch(R_out), .Bottom_Door_Switch(D_out), .Left_Door_Switch(L_out),
    .Top_Door_choosen(roomdatainterface_1_top_door_choosen),
    .Right_Door_choosen(roomdatainterface_1_right_door_choosen),
    .Bottom_Door_choosen(roomdatainterface_1_bottom_door_choosen),
    .Left_Door_choosen(roomdatainterface_1_left_door_choosen), .Door_Data(Manual_Data));
  DotMatrix #(.inputtype("row"), .matrixcols(32), .matrixrows(32)) dotmatrix_4 (
    .row0(n64x64_led_control_1_out_25), .row1(n64x64_led_control_1_out_26),
    .row2(n64x64_led_control_1_out_27), .row3(n64x64_led_control_1_out_28),
    .row4(n64x64_led_control_1_out_29), .row5(n64x64_led_control_1_out_30),
    .row6(n64x64_led_control_1_out_31), .row7(n64x64_led_control_1_out_32),
    .row8(n64x64_led_control_1_out_41), .row9(n64x64_led_control_1_out_42),
    .row10(n64x64_led_control_1_out_43), .row11(n64x64_led_control_1_out_44),
    .row12(n64x64_led_control_1_out_45), .row13(n64x64_led_control_1_out_46),
    .row14(n64x64_led_control_1_out_47), .row15(n64x64_led_control_1_out_48),
    .row16(n64x64_led_control_1_out_57), .row17(n64x64_led_control_1_out_58),
    .row18(n64x64_led_control_1_out_59), .row19(n64x64_led_control_1_out_60),
    .row20(n64x64_led_control_1_out_61), .row21(n64x64_led_control_1_out_62),
    .row22(n64x64_led_control_1_out_63), .row23(n64x64_led_control_1_out_64),
    .row24(n64x64_led_control_1_out_73), .row25(n64x64_led_control_1_out_74),
    .row26(n64x64_led_control_1_out_75), .row27(n64x64_led_control_1_out_76),
    .row28(n64x64_led_control_1_out_77), .row29(n64x64_led_control_1_out_78),
    .row30(n64x64_led_control_1_out_79), .row31(n64x64_led_control_1_out_80));
  DotMatrix #(.inputtype("row"), .matrixcols(32), .matrixrows(32)) dotmatrix_5 (
    .row0(n64x64_led_control_1_out_89), .row1(n64x64_led_control_1_out_90),
    .row2(n64x64_led_control_1_out_91), .row3(n64x64_led_control_1_out_92),
    .row4(n64x64_led_control_1_out_93), .row5(n64x64_led_control_1_out_94),
    .row6(n64x64_led_control_1_out_95), .row7(n64x64_led_control_1_out_96),
    .row8(n64x64_led_control_1_out_105), .row9(n64x64_led_control_1_out_106),
    .row10(n64x64_led_control_1_out_107), .row11(n64x64_led_control_1_out_108),
    .row12(n64x64_led_control_1_out_109), .row13(n64x64_led_control_1_out_110),
    .row14(n64x64_led_control_1_out_111), .row15(n64x64_led_control_1_out_112),
    .row16(n64x64_led_control_1_out_121), .row17(n64x64_led_control_1_out_122),
    .row18(n64x64_led_control_1_out_123), .row19(n64x64_led_control_1_out_124),
    .row20(n64x64_led_control_1_out_125), .row21(n64x64_led_control_1_out_126),
    .row22(n64x64_led_control_1_out_127), .row23(n64x64_led_control_1_out_128),
    .row24(n64x64_led_control_1_out_137), .row25(n64x64_led_control_1_out_138),
    .row26(n64x64_led_control_1_out_139), .row27(n64x64_led_control_1_out_140),
    .row28(n64x64_led_control_1_out_141), .row29(n64x64_led_control_1_out_142),
    .row30(n64x64_led_control_1_out_143), .row31(n64x64_led_control_1_out_144));
  _64x64_LED_Control u_64x64_led_control_1 (
    .CLK(CLK), .RST(Reset), .out_17(n64x64_led_control_1_out_17), .out_18(n64x64_led_control_1_out_18),
    .out_19(n64x64_led_control_1_out_19), .out_20(n64x64_led_control_1_out_20),
    .out_21(n64x64_led_control_1_out_21), .out_22(n64x64_led_control_1_out_22),
    .out_23(n64x64_led_control_1_out_23), .out_24(n64x64_led_control_1_out_24),
    .out_25(n64x64_led_control_1_out_25), .out_26(n64x64_led_control_1_out_26),
    .out_27(n64x64_led_control_1_out_27), .out_28(n64x64_led_control_1_out_28),
    .out_29(n64x64_led_control_1_out_29), .out_30(n64x64_led_control_1_out_30),
    .out_31(n64x64_led_control_1_out_31), .out_32(n64x64_led_control_1_out_32),
    .out_33(n64x64_led_control_1_out_33), .out_34(n64x64_led_control_1_out_34),
    .out_35(n64x64_led_control_1_out_35), .out_36(n64x64_led_control_1_out_36),
    .out_37(n64x64_led_control_1_out_37), .out_38(n64x64_led_control_1_out_38),
    .out_39(n64x64_led_control_1_out_39), .out_40(n64x64_led_control_1_out_40),
    .out_41(n64x64_led_control_1_out_41), .out_42(n64x64_led_control_1_out_42),
    .out_43(n64x64_led_control_1_out_43), .out_44(n64x64_led_control_1_out_44),
    .out_45(n64x64_led_control_1_out_45), .out_46(n64x64_led_control_1_out_46),
    .out_47(n64x64_led_control_1_out_47), .out_48(n64x64_led_control_1_out_48),
    .out_49(n64x64_led_control_1_out_49), .out_50(n64x64_led_control_1_out_50),
    .out_51(n64x64_led_control_1_out_51), .out_52(n64x64_led_control_1_out_52),
    .out_53(n64x64_led_control_1_out_53), .out_54(n64x64_led_control_1_out_54),
    .out_55(n64x64_led_control_1_out_55), .out_56(n64x64_led_control_1_out_56),
    .out_57(n64x64_led_control_1_out_57), .out_58(n64x64_led_control_1_out_58),
    .out_59(n64x64_led_control_1_out_59), .out_60(n64x64_led_control_1_out_60),
    .out_61(n64x64_led_control_1_out_61), .out_62(n64x64_led_control_1_out_62),
    .out_63(n64x64_led_control_1_out_63), .out_64(n64x64_led_control_1_out_64),
    .out_65(n64x64_led_control_1_out_65), .out_66(n64x64_led_control_1_out_66),
    .out_67(n64x64_led_control_1_out_67), .out_68(n64x64_led_control_1_out_68),
    .out_69(n64x64_led_control_1_out_69), .out_70(n64x64_led_control_1_out_70),
    .out_71(n64x64_led_control_1_out_71), .out_72(n64x64_led_control_1_out_72),
    .out_73(n64x64_led_control_1_out_73), .out_74(n64x64_led_control_1_out_74),
    .out_75(n64x64_led_control_1_out_75), .out_76(n64x64_led_control_1_out_76),
    .out_77(n64x64_led_control_1_out_77), .out_78(n64x64_led_control_1_out_78),
    .out_79(n64x64_led_control_1_out_79), .out_80(n64x64_led_control_1_out_80),
    .out_81(n64x64_led_control_1_out_81), .out_82(n64x64_led_control_1_out_82),
    .out_83(n64x64_led_control_1_out_83), .out_84(n64x64_led_control_1_out_84),
    .out_85(n64x64_led_control_1_out_85), .out_86(n64x64_led_control_1_out_86),
    .out_87(n64x64_led_control_1_out_87), .out_88(n64x64_led_control_1_out_88),
    .out_89(n64x64_led_control_1_out_89), .out_90(n64x64_led_control_1_out_90),
    .out_91(n64x64_led_control_1_out_91), .out_92(n64x64_led_control_1_out_92),
    .out_93(n64x64_led_control_1_out_93), .out_94(n64x64_led_control_1_out_94),
    .out_95(n64x64_led_control_1_out_95), .out_96(n64x64_led_control_1_out_96),
    .out_97(n64x64_led_control_1_out_97), .out_98(n64x64_led_control_1_out_98),
    .out_99(n64x64_led_control_1_out_99), .out_100(n64x64_led_control_1_out_100),
    .out_101(n64x64_led_control_1_out_101), .out_102(n64x64_led_control_1_out_102),
    .out_103(n64x64_led_control_1_out_103), .out_104(n64x64_led_control_1_out_104),
    .out_105(n64x64_led_control_1_out_105), .out_106(n64x64_led_control_1_out_106),
    .out_107(n64x64_led_control_1_out_107), .out_108(n64x64_led_control_1_out_108),
    .out_109(n64x64_led_control_1_out_109), .out_110(n64x64_led_control_1_out_110),
    .out_111(n64x64_led_control_1_out_111), .out_112(n64x64_led_control_1_out_112),
    .out_113(n64x64_led_control_1_out_113), .out_114(n64x64_led_control_1_out_114),
    .out_115(n64x64_led_control_1_out_115), .out_116(n64x64_led_control_1_out_116),
    .out_117(n64x64_led_control_1_out_117), .out_118(n64x64_led_control_1_out_118),
    .out_119(n64x64_led_control_1_out_119), .out_120(n64x64_led_control_1_out_120),
    .out_121(n64x64_led_control_1_out_121), .out_122(n64x64_led_control_1_out_122),
    .out_123(n64x64_led_control_1_out_123), .out_124(n64x64_led_control_1_out_124),
    .out_125(n64x64_led_control_1_out_125), .out_126(n64x64_led_control_1_out_126),
    .out_127(n64x64_led_control_1_out_127), .out_128(n64x64_led_control_1_out_128),
    .out_129(n64x64_led_control_1_out_129), .out_130(n64x64_led_control_1_out_130),
    .out_131(n64x64_led_control_1_out_131), .out_132(n64x64_led_control_1_out_132),
    .out_133(n64x64_led_control_1_out_133), .out_134(n64x64_led_control_1_out_134),
    .out_135(n64x64_led_control_1_out_135), .out_136(n64x64_led_control_1_out_136),
    .out_137(n64x64_led_control_1_out_137), .out_138(n64x64_led_control_1_out_138),
    .out_139(n64x64_led_control_1_out_139), .out_140(n64x64_led_control_1_out_140),
    .out_141(n64x64_led_control_1_out_141), .out_142(n64x64_led_control_1_out_142),
    .out_143(n64x64_led_control_1_out_143), .out_144(n64x64_led_control_1_out_144), .in_9(program_1_out_19),
    .in_10(program_1_out_16), .in_11(program_1_out_14), .in_12(program_1_out_13), .in_13(program_1_out_12),
    .in_14(program_1_out_11), .in_15(program_1_out_10), .in_16(program_1_out_9), .in_1(main_2_out_2),
    .Initial_Position(sefe_start_calc_1_safe_pixel_address), .input_Clock(CLK), .isGame(in_2),
    .Keyboard_input(key_out), .FINISHED(Algorithm_Finished));
  LED led_3 (.in(roomdatainterface_1_top_door_choosen));
  LED led_4 (.in(roomdatainterface_1_left_door_choosen));
  LED led_5 (.in(roomdatainterface_1_bottom_door_choosen));
  LED led_6 (.in(roomdatainterface_1_right_door_choosen));
  and and_1 (and_1_out, Room_Design, ~in_2);  // AND_Gate
  wybieracz_pokoi_main main_2 (.in_1(and_1_out), .out_2(main_2_out_2));
  Keyboard #(.buflen(2)) keyboard_1 (.clk(CLK), .data(key_out));  // open: re, clr, avail

  // Other names for the same wires on the sheet: GAMING = in_2; Manual_Write = in_1

  // Notes on the sheet:
  //   INSTRUCTION
  //   Control Algorithm
  //   Reset 
  //   Change room design (Cursor must be disabled to use)
  //   - You can edit rooms manually using menu below
  //   - You can test the generated layout using a moving cursor
  //   - Program generates random room layout and displays it on LED Matrix
  //   (Recommended amount of rooms is between 16 - 32, otherwise program might not work correctly)
  //   Column
  //   - Choose the amount of rooms to generate and click Algorithm Init button to start generating
  //   Manual Room Edit
  //   Allows you to edit rooms manually
  //   1. Choose Room location
  //   Row
  //   To see the effects you have to disable manual write
  //   2. Choose the room's exits (if all exits are disabled empty room will be created)
  //   3. Enable Manual Write using the switch, apply changes using thepink button below
  //   Moving Cursor Control
  //   Enable moving cursor
  //   Control using WSAD
endmodule

module Program (
  input  Manual_Write,
  input  Manual_Write_CLK,
  input  [3:0] Manual_Data,
  input  [5:0] Manual_Address,
  input  RAM_Manual_RST,
  input  Algorithm_Init,
  input  [7:0] Room_Limit,
  input  CLK,
  output [31:0] out_9,
  output [31:0] out_10,
  output [31:0] out_11,
  output [31:0] out_12,
  output [31:0] out_13,
  output [31:0] out_14,
  output out_15,
  output [31:0] out_16,
  output out_17,
  output [5:0] out_18,
  output [31:0] out_19
);

  wire Algorithm_RAM_CLK, Algorithm_Write, and_1_out, and_2_out, and_3_out, controlled_buffer_6_out,
       controlled_buffer_8_out, not_1_out, not_2_out, not_3_out, or_1_out, RAM_Reset;
  wire [3:0] Algorithm_Data, controlled_buffer_1_out, RAM_Data;
  wire [5:0] Algorithm_Address, controlled_buffer_3_out, LED_Control_Address;
  wire [31:0] roommemory_1_out_6;

  Algorithm_main main_1 (
    .RAM_Write(Algorithm_Write), .RAM_CLK(Algorithm_RAM_CLK), .Ram_Clear(RAM_Reset), .START(Algorithm_Init),
    .RAM_Address(Algorithm_Address), .Safe_Room(out_18), .Room_Limit(Room_Limit), .CLK(CLK),
    .Running(out_15), .Finished(out_17), .RAM_Data(Algorithm_Data), .RAM_Read_Data(RAM_Data));
  assign controlled_buffer_1_out = and_1_out ? Manual_Data : 4'bz;  // Controlled_Buffer controlled_buffer_1
  and and_1 (and_1_out, Manual_Write, ~out_15);  // AND_Gate
  assign controlled_buffer_1_out = out_15 ? Algorithm_Data : 4'bz;  // Controlled_Buffer controlled_buffer_2
  and and_2 (and_2_out, Manual_Write, ~out_15);  // AND_Gate
  Pull_Resistor pull_resistor_1 (.node(controlled_buffer_1_out));
  assign controlled_buffer_3_out = and_2_out ? Manual_Address : 6'bz;  // Controlled_Buffer controlled_buffer_3
  assign controlled_buffer_3_out = and_3_out ? LED_Control_Address : 6'bz;  // Controlled_Buffer controlled_buffer_4
  and and_3 (and_3_out, ~Manual_Write, ~out_15);  // AND_Gate
  assign controlled_buffer_3_out = out_15 ? Algorithm_Address : 6'bz;  // Controlled_Buffer controlled_buffer_5
  assign controlled_buffer_6_out = not_1_out ? Manual_Write : 1'bz;  // Controlled_Buffer controlled_buffer_6
  not not_1 (not_1_out, out_15);
  assign controlled_buffer_6_out = out_15 ? Algorithm_Write : 1'bz;  // Controlled_Buffer controlled_buffer_7
  assign controlled_buffer_8_out = not_2_out ? Manual_Write_CLK : 1'bz;  // Controlled_Buffer controlled_buffer_8
  not not_2 (not_2_out, out_15);
  assign controlled_buffer_8_out = out_15 ? Algorithm_RAM_CLK : 1'bz;  // Controlled_Buffer controlled_buffer_9
  or or_1 (or_1_out, RAM_Reset, RAM_Manual_RST);
  roomMemory roommemory_1 (
    .CLK(controlled_buffer_8_out), .Write(controlled_buffer_6_out), .D(controlled_buffer_1_out),
    .out_7(RAM_Data), .out_6(roommemory_1_out_6), .Reset(or_1_out), .A(controlled_buffer_3_out));
  memoryReadControl memoryreadcontrol_1 (
    .CLK(CLK), .Write(not_3_out), .Data(roommemory_1_out_6), .A(LED_Control_Address), .out_4(out_9),
    .out_6(out_10), .out_7(out_11), .out_8(out_12), .out_9(out_13), .out_10(out_14), .out_11(out_16),
    .out_12(out_19));
  not not_3 (not_3_out, Manual_Write);

  // Other names for the same wires on the sheet: Algorithm_Finished = out_17; Algorithm_Running = out_15;
  //   RAM_Manual_Reset = RAM_Manual_RST; Safe_Room[5:0] = out_18

  // Notes on the sheet:
  //   8x Room Control Output
endmodule

module roomDataInterface (
  input  Top_Door_Switch,
  input  Right_Door_Switch,
  input  Bottom_Door_Switch,
  input  Left_Door_Switch,
  output Top_Door_choosen,
  output Right_Door_choosen,
  output Bottom_Door_choosen,
  output Left_Door_choosen,
  output [3:0] Door_Data
);

  Counter #(.width(1), .max('h1)) counter_1 (
    .Q(Door_Data[3]), .clk(Top_Door_Switch));  // open: load, D, count, carry, clr
  Counter #(.width(1), .max('h1)) counter_2 (
    .Q(Door_Data[2]), .clk(Right_Door_Switch));  // open: load, D, count, carry, clr
  Counter #(.width(1), .max('h1)) counter_3 (
    .Q(Bottom_Door_choosen), .clk(Bottom_Door_Switch));  // open: load, D, count, carry, clr
  Counter #(.width(1), .max('h1)) counter_4 (
    .Q(Door_Data[0]), .clk(Left_Door_Switch));  // open: load, D, count, carry, clr

  assign Door_Data[1] = Bottom_Door_choosen;
  assign Left_Door_choosen = Door_Data[0];
  assign Right_Door_choosen = Door_Data[2];
  assign Top_Door_choosen = Door_Data[3];
endmodule
