// Logisim project MovementLogic.circ as structural Verilog: 9 circuits, main circuit main
module main (
);

  _12_bit_selector u_12_bit_selector_1 ();  // open: Select, in_10, in_26, in_42, in_58, in_74, in_90, in_106, in_122, in_11, in_27, in_43, in_59, in_75, in_91, in_107, in_123, Probed_bit, in_12, in_28, in_44, in_60, in_76, in_92, in_108, in_124, in_13, in_29, in_45, in_61, in_77, in_93, in_109, in_125, in_14, in_30, in_46, in_62, in_78, in_94, in_110, in_126, in_15, in_31, in_47, in_63, in_79, in_95, in_111, in_127, in_16, in_32, in_48, in_64, in_80, in_96, in_112, in_128, in_17, in_33, in_49, in_65, in_81, in_97, in_113, in_129, in_2, in_3, in_4, in_5, in_6, in_7, in_8, in_9, in_18, in_19, in_20, in_21, in_22, in_23, in_24, in_25, in_34, in_35, in_36, in_37, in_38, in_39, in_40, in_41, in_50, in_51, in_52, in_53, in_54, in_55, in_56, in_57, in_66, in_67, in_68, in_69, in_70, in_71, in_72, in_73, in_82, in_83, in_84, in_85, in_86, in_87, in_88, in_89, in_98, in_99, in_100, in_101, in_102, in_103, in_104, in_105, in_114, in_115, in_116, in_117, in_118, in_119, in_120, in_121
endmodule

module _6_bit_selector (
  input  [31:0] In__first_32,
  input  [5:0] Select,
  input  [31:0] In__second_32,
  output out_4
);

  wire [1:0] bitselector_1_out;
  wire [4:0] not_1_out;

  assign not_1_out = ~Select[4:0];  // NOT_Gate not_1, 5 bits wide
  BitSelector #(.width(32)) bitselector_1 (.in(In__first_32), .out(bitselector_1_out[0]), .sel(not_1_out));
  BitSelector #(.width(32)) bitselector_2 (.in(In__second_32), .out(bitselector_1_out[1]), .sel(not_1_out));
  BitSelector #(.width(2)) bitselector_3 (.in(bitselector_1_out), .out(out_4), .sel(Select[5]));
endmodule

module _12_bit_selector (
  input  [11:0] Select,
  input  [31:0] in_2,
  input  [31:0] in_3,
  input  [31:0] in_4,
  input  [31:0] in_5,
  input  [31:0] in_6,
  input  [31:0] in_7,
  input  [31:0] in_8,
  input  [31:0] in_9,
  input  [31:0] in_10,
  input  [31:0] in_11,
  input  [31:0] in_12,
  input  [31:0] in_13,
  input  [31:0] in_14,
  input  [31:0] in_15,
  input  [31:0] in_16,
  input  [31:0] in_17,
  input  [31:0] in_18,
  input  [31:0] in_19,
  input  [31:0] in_20,
  input  [31:0] in_21,
  input  [31:0] in_22,
  input  [31:0] in_23,
  input  [31:0] in_24,
  input  [31:0] in_25,
  input  [31:0] in_26,
  input  [31:0] in_27,
  input  [31:0] in_28,
  input  [31:0] in_29,
  input  [31:0] in_30,
  input  [31:0] in_31,
  input  [31:0] in_32,
  input  [31:0] in_33,
  input  [31:0] in_34,
  input  [31:0] in_35,
  input  [31:0] in_36,
  input  [31:0] in_37,
  input  [31:0] in_38,
  input  [31:0] in_39,
  input  [31:0] in_40,
  input  [31:0] in_41,
  input  [31:0] in_42,
  input  [31:0] in_43,
  input  [31:0] in_44,
  input  [31:0] in_45,
  input  [31:0] in_46,
  input  [31:0] in_47,
  input  [31:0] in_48,
  input  [31:0] in_49,
  input  [31:0] in_50,
  input  [31:0] in_51,
  input  [31:0] in_52,
  input  [31:0] in_53,
  input  [31:0] in_54,
  input  [31:0] in_55,
  input  [31:0] in_56,
  input  [31:0] in_57,
  input  [31:0] in_58,
  input  [31:0] in_59,
  input  [31:0] in_60,
  input  [31:0] in_61,
  input  [31:0] in_62,
  input  [31:0] in_63,
  input  [31:0] in_64,
  input  [31:0] in_65,
  input  [31:0] in_66,
  input  [31:0] in_67,
  input  [31:0] in_68,
  input  [31:0] in_69,
  input  [31:0] in_70,
  input  [31:0] in_71,
  input  [31:0] in_72,
  input  [31:0] in_73,
  input  [31:0] in_74,
  input  [31:0] in_75,
  input  [31:0] in_76,
  input  [31:0] in_77,
  input  [31:0] in_78,
  input  [31:0] in_79,
  input  [31:0] in_80,
  input  [31:0] in_81,
  input  [31:0] in_82,
  input  [31:0] in_83,
  input  [31:0] in_84,
  input  [31:0] in_85,
  input  [31:0] in_86,
  input  [31:0] in_87,
  input  [31:0] in_88,
  input  [31:0] in_89,
  input  [31:0] in_90,
  input  [31:0] in_91,
  input  [31:0] in_92,
  input  [31:0] in_93,
  input  [31:0] in_94,
  input  [31:0] in_95,
  input  [31:0] in_96,
  input  [31:0] in_97,
  input  [31:0] in_98,
  input  [31:0] in_99,
  input  [31:0] in_100,
  input  [31:0] in_101,
  input  [31:0] in_102,
  input  [31:0] in_103,
  input  [31:0] in_104,
  input  [31:0] in_105,
  input  [31:0] in_106,
  input  [31:0] in_107,
  input  [31:0] in_108,
  input  [31:0] in_109,
  input  [31:0] in_110,
  input  [31:0] in_111,
  input  [31:0] in_112,
  input  [31:0] in_113,
  input  [31:0] in_114,
  input  [31:0] in_115,
  input  [31:0] in_116,
  input  [31:0] in_117,
  input  [31:0] in_118,
  input  [31:0] in_119,
  input  [31:0] in_120,
  input  [31:0] in_121,
  input  [31:0] in_122,
  input  [31:0] in_123,
  input  [31:0] in_124,
  input  [31:0] in_125,
  input  [31:0] in_126,
  input  [31:0] in_127,
  input  [31:0] in_128,
  input  [31:0] in_129,
  output Probed_bit
);

  wire [1:0] bitselector_2_out;
  wire [31:0] out_low, out_up;

  _6_bit_selector u_6_bit_selector_1 (
    .In__first_32(in_10), .Select(Select[5:0]), .In__second_32(in_11), .out_4(out_low[0]));
  _6_bit_selector u_6_bit_selector_2 (
    .In__first_32(in_26), .Select(Select[5:0]), .In__second_32(in_27), .out_4(out_low[1]));
  _6_bit_selector u_6_bit_selector_3 (
    .In__first_32(in_42), .Select(Select[5:0]), .In__second_32(in_43), .out_4(out_low[2]));
  _6_bit_selector u_6_bit_selector_4 (
    .In__first_32(in_58), .Select(Select[5:0]), .In__second_32(in_59), .out_4(out_low[3]));
  _6_bit_selector u_6_bit_selector_5 (
    .In__first_32(in_74), .Select(Select[5:0]), .In__second_32(in_75), .out_4(out_low[4]));
  _6_bit_selector u_6_bit_selector_6 (
    .In__first_32(in_90), .Select(Select[5:0]), .In__second_32(in_91), .out_4(out_low[5]));
  _6_bit_selector u_6_bit_selector_7 (
    .In__first_32(in_106), .Select(Select[5:0]), .In__second_32(in_107), .out_4(out_low[6]));
  _6_bit_selector u_6_bit_selector_8 (
    .In__first_32(in_122), .Select(Select[5:0]), .In__second_32(in_123), .out_4(out_low[7]));
  BitSelector #(.width(2)) bitselector_1 (.in(bitselector_2_out), .out(Probed_bit), .sel(Select[11]));
  BitSelector #(.width(32)) bitselector_2 (.in(out_low), .out(bitselector_2_out[0]), .sel(Select[10:6]));
  BitSelector #(.width(32)) bitselector_3 (.in(out_up), .out(bitselector_2_out[1]), .sel(Select[10:6]));
  _6_bit_selector u_6_bit_selector_9 (
    .In__first_32(in_12), .Select(Select[5:0]), .In__second_32(in_13), .out_4(out_low[8]));
  _6_bit_selector u_6_bit_selector_10 (
    .In__first_32(in_28), .Select(Select[5:0]), .In__second_32(in_29), .out_4(out_low[9]));
  _6_bit_selector u_6_bit_selector_11 (
    .In__first_32(in_44), .Select(Select[5:0]), .In__second_32(in_45), .out_4(out_low[10]));
  _6_bit_selector u_6_bit_selector_12 (
    .In__first_32(in_60), .Select(Select[5:0]), .In__second_32(in_61), .out_4(out_low[11]));
  _6_bit_selector u_6_bit_selector_13 (
    .In__first_32(in_76), .Select(Select[5:0]), .In__second_32(in_77), .out_4(out_low[12]));
  _6_bit_selector u_6_bit_selector_14 (
    .In__first_32(in_92), .Select(Select[5:0]), .In__second_32(in_93), .out_4(out_low[13]));
  _6_bit_selector u_6_bit_selector_15 (
    .In__first_32(in_108), .Select(Select[5:0]), .In__second_32(in_109), .out_4(out_low[14]));
  _6_bit_selector u_6_bit_selector_16 (
    .In__first_32(in_124), .Select(Select[5:0]), .In__second_32(in_125), .out_4(out_low[15]));
  _6_bit_selector u_6_bit_selector_17 (
    .In__first_32(in_14), .Select(Select[5:0]), .In__second_32(in_15), .out_4(out_low[16]));
  _6_bit_selector u_6_bit_selector_18 (
    .In__first_32(in_30), .Select(Select[5:0]), .In__second_32(in_31), .out_4(out_low[17]));
  _6_bit_selector u_6_bit_selector_19 (
    .In__first_32(in_46), .Select(Select[5:0]), .In__second_32(in_47), .out_4(out_low[18]));
  _6_bit_selector u_6_bit_selector_20 (
    .In__first_32(in_62), .Select(Select[5:0]), .In__second_32(in_63), .out_4(out_low[19]));
  _6_bit_selector u_6_bit_selector_21 (
    .In__first_32(in_78), .Select(Select[5:0]), .In__second_32(in_79), .out_4(out_low[20]));
  _6_bit_selector u_6_bit_selector_22 (
    .In__first_32(in_94), .Select(Select[5:0]), .In__second_32(in_95), .out_4(out_low[21]));
  _6_bit_selector u_6_bit_selector_23 (
    .In__first_32(in_110), .Select(Select[5:0]), .In__second_32(in_111), .out_4(out_low[22]));
  _6_bit_selector u_6_bit_selector_24 (
    .In__first_32(in_126), .Select(Select[5:0]), .In__second_32(in_127), .out_4(out_low[23]));
  _6_bit_selector u_6_bit_selector_25 (
    .In__first_32(in_16), .Select(Select[5:0]), .In__second_32(in_17), .out_4(out_low[24]));
  _6_bit_selector u_6_bit_selector_26 (
    .In__first_32(in_32), .Select(Select[5:0]), .In__second_32(in_33), .out_4(out_low[25]));
  _6_bit_selector u_6_bit_selector_27 (
    .In__first_32(in_48), .Select(Select[5:0]), .In__second_32(in_49), .out_4(out_low[26]));
  _6_bit_selector u_6_bit_selector_28 (
    .In__first_32(in_64), .Select(Select[5:0]), .In__second_32(in_65), .out_4(out_low[27]));
  _6_bit_selector u_6_bit_selector_29 (
    .In__first_32(in_80), .Select(Select[5:0]), .In__second_32(in_81), .out_4(out_low[28]));
  _6_bit_selector u_6_bit_selector_30 (
    .In__first_32(in_96), .Select(Select[5:0]), .In__second_32(in_97), .out_4(out_low[29]));
  _6_bit_selector u_6_bit_selector_31 (
    .In__first_32(in_112), .Select(Select[5:0]), .In__second_32(in_113), .out_4(out_low[30]));
  _6_bit_selector u_6_bit_selector_32 (
    .In__first_32(in_128), .Select(Select[5:0]), .In__second_32(in_129), .out_4(out_low[31]));
  _6_bit_selector u_6_bit_selector_33 (
    .In__first_32(in_2), .Select(Select[5:0]), .In__second_32(in_3), .out_4(out_up[0]));
  _6_bit_selector u_6_bit_selector_34 (
    .In__first_32(in_18), .Select(Select[5:0]), .In__second_32(in_19), .out_4(out_up[1]));
  _6_bit_selector u_6_bit_selector_35 (
    .In__first_32(in_34), .Select(Select[5:0]), .In__second_32(in_35), .out_4(out_up[2]));
  _6_bit_selector u_6_bit_selector_36 (
    .In__first_32(in_50), .Select(Select[5:0]), .In__second_32(in_51), .out_4(out_up[3]));
  _6_bit_selector u_6_bit_selector_37 (
    .In__first_32(in_66), .Select(Select[5:0]), .In__second_32(in_67), .out_4(out_up[4]));
  _6_bit_selector u_6_bit_selector_38 (
    .In__first_32(in_82), .Select(Select[5:0]), .In__second_32(in_83), .out_4(out_up[5]));
  _6_bit_selector u_6_bit_selector_39 (
    .In__first_32(in_98), .Select(Select[5:0]), .In__second_32(in_99), .out_4(out_up[6]));
  _6_bit_selector u_6_bit_selector_40 (
    .In__first_32(in_114), .Select(Select[5:0]), .In__second_32(in_115), .out_4(out_up[7]));
  _6_bit_selector u_6_bit_selector_41 (
    .In__first_32(in_4), .Select(Select[5:0]), .In__second_32(in_5), .out_4(out_up[8]));
  _6_bit_selector u_6_bit_selector_42 (
    .In__first_32(in_20), .Select(Select[5:0]), .In__second_32(in_21), .out_4(out_up[9]));
  _6_bit_selector u_6_bit_selector_43 (
    .In__first_32(in_36), .Select(Select[5:0]), .In__second_32(in_37), .out_4(out_up[10]));
  _6_bit_selector u_6_bit_selector_44 (
    .In__first_32(in_52), .Select(Select[5:0]), .In__second_32(in_53), .out_4(out_up[11]));
  _6_bit_selector u_6_bit_selector_45 (
    .In__first_32(in_68), .Select(Select[5:0]), .In__second_32(in_69), .out_4(out_up[12]));
  _6_bit_selector u_6_bit_selector_46 (
    .In__first_32(in_84), .Select(Select[5:0]), .In__second_32(in_85), .out_4(out_up[13]));
  _6_bit_selector u_6_bit_selector_47 (
    .In__first_32(in_100), .Select(Select[5:0]), .In__second_32(in_101), .out_4(out_up[14]));
  _6_bit_selector u_6_bit_selector_48 (
    .In__first_32(in_116), .Select(Select[5:0]), .In__second_32(in_117), .out_4(out_up[15]));
  _6_bit_selector u_6_bit_selector_49 (
    .In__first_32(in_6), .Select(Select[5:0]), .In__second_32(in_7), .out_4(out_up[16]));
  _6_bit_selector u_6_bit_selector_50 (
    .In__first_32(in_22), .Select(Select[5:0]), .In__second_32(in_23), .out_4(out_up[17]));
  _6_bit_selector u_6_bit_selector_51 (
    .In__first_32(in_38), .Select(Select[5:0]), .In__second_32(in_39), .out_4(out_up[18]));
  _6_bit_selector u_6_bit_selector_52 (
    .In__first_32(in_54), .Select(Select[5:0]), .In__second_32(in_55), .out_4(out_up[19]));
  _6_bit_selector u_6_bit_selector_53 (
    .In__first_32(in_70), .Select(Select[5:0]), .In__second_32(in_71), .out_4(out_up[20]));
  _6_bit_selector u_6_bit_selector_54 (
    .In__first_32(in_86), .Select(Select[5:0]), .In__second_32(in_87), .out_4(out_up[21]));
  _6_bit_selector u_6_bit_selector_55 (
    .In__first_32(in_102), .Select(Select[5:0]), .In__second_32(in_103), .out_4(out_up[22]));
  _6_bit_selector u_6_bit_selector_56 (
    .In__first_32(in_118), .Select(Select[5:0]), .In__second_32(in_119), .out_4(out_up[23]));
  _6_bit_selector u_6_bit_selector_57 (
    .In__first_32(in_8), .Select(Select[5:0]), .In__second_32(in_9), .out_4(out_up[24]));
  _6_bit_selector u_6_bit_selector_58 (
    .In__first_32(in_24), .Select(Select[5:0]), .In__second_32(in_25), .out_4(out_up[25]));
  _6_bit_selector u_6_bit_selector_59 (
    .In__first_32(in_40), .Select(Select[5:0]), .In__second_32(in_41), .out_4(out_up[26]));
  _6_bit_selector u_6_bit_selector_60 (
    .In__first_32(in_56), .Select(Select[5:0]), .In__second_32(in_57), .out_4(out_up[27]));
  _6_bit_selector u_6_bit_selector_61 (
    .In__first_32(in_72), .Select(Select[5:0]), .In__second_32(in_73), .out_4(out_up[28]));
  _6_bit_selector u_6_bit_selector_62 (
    .In__first_32(in_88), .Select(Select[5:0]), .In__second_32(in_89), .out_4(out_up[29]));
  _6_bit_selector u_6_bit_selector_63 (
    .In__first_32(in_104), .Select(Select[5:0]), .In__second_32(in_105), .out_4(out_up[30]));
  _6_bit_selector u_6_bit_selector_64 (
    .In__first_32(in_120), .Select(Select[5:0]), .In__second_32(in_121), .out_4(out_up[31]));

  // Other names for the same wires on the sheet: sel_low[5:0] = Select[5:0]
endmodule

module movement_check (
  input  [2:0] Movement_direction,
  input  [11:0] Current_position,
  output [11:0] New_location,
  output Overflow_flag
);

  wire f_down, f_left, f_right, f_up, multiplexer_2_out;
  wire [11:0] down, left, multiplexer_1_out, right, up;

  Adder #(.width(12)) adder_1 (.a(Current_position), .b(12'h40), .out(down), .cout(f_down));  // open: cin
  Subtractor #(.width(12)) subtractor_1 (.a(Current_position), .b(12'h40), .out(up), .bout(f_up));  // open: bin
  Adder #(.width(12)) adder_2 (.a(Current_position), .b(12'h1), .out(right));  // open: cin, cout
  Subtractor #(.width(12)) subtractor_2 (.a(Current_position), .b(12'h1), .out(left));  // open: bin, bout
  check_horizontal_overflow check_horizontal_overflow_1 (.in_1(right), .in_2(Current_position), .out_3(f_right));
  check_horizontal_overflow check_horizontal_overflow_2 (.in_1(left), .in_2(Current_position), .out_3(f_left));
  Multiplexer #(.select(2), .width(12)) multiplexer_1 (
    .in0(up), .in1(right), .in2(down), .in3(left), .out(multiplexer_1_out), .sel(Movement_direction[1:0]));  // open: en
  Multiplexer #(.select(2)) multiplexer_2 (
    .in0(f_up), .in1(f_right), .in2(f_down), .in3(f_left), .out(multiplexer_2_out),
    .sel(Movement_direction[1:0]));  // open: en
  Multiplexer #(.width(12)) multiplexer_3 (
    .in0(Current_position), .in1(multiplexer_1_out), .out(New_location), .sel(Movement_direction[2]));  // open: en
  and and_1 (Overflow_flag, multiplexer_2_out, Movement_direction[2]);

  // Other names for the same wires on the sheet: current[11:0] = Current_position; dir[1:0] = Movement_direction[1:0];
  //   isMove = Movement_direction[2]
endmodule

module check_horizontal_overflow (
  input  [11:0] in_1,
  input  [11:0] in_2,
  output out_3
);

  wire comparator_1_eq, comparator_2_eq, not_2_out;
  wire [5:0] not_1_out, xor_1_out, xor_2_out;

  assign xor_1_out = in_1[11:6] ^ in_2[11:6];  // XOR_Gate xor_1, 6 bits wide
  Comparator #(.width(6)) comparator_1 (.a({6{1'b0}}), .b(xor_2_out), .eq(comparator_1_eq));  // open: gt, lt
  assign xor_2_out = in_1[5:0] ^ not_1_out;  // XOR_Gate xor_2, 6 bits wide
  assign not_1_out = ~in_2[5:0];  // NOT_Gate not_1, 6 bits wide
  not not_2 (not_2_out, comparator_2_eq);
  Comparator #(.width(6)) comparator_2 (.a({6{1'b0}}), .b(xor_1_out), .eq(comparator_2_eq));  // open: gt, lt
  and and_1 (out_3, comparator_1_eq, not_2_out);
endmodule

module movement_procesing (
  input  [11:0] in_1,
  input  in_2,
  output [2:0] out_3
);

  wire and_1_out, Clock_input, isBlocked, movement_check_1_overflow_flag, not_1_out, or_1_out;
  wire [6:0] keyboard_1_data;
  wire [11:0] Current_location, multiplexer_1_out, New_location, register_1_q;

  Clock clock_1 (.out(Clock_input));
  Keyboard #(.buflen(1)) keyboard_1 (.clk(Clock_input), .data(keyboard_1_data));  // open: re, clr, avail
  ROM #(.addrWidth(7), .dataWidth(3)) rom_1 (.addr(keyboard_1_data), .data(out_3));  // open: sel
  _12_bit_selector u_12_bit_selector_1 (
    .Select(New_location), .Probed_bit(isBlocked));  // open: in_10, in_26, in_42, in_58, in_74, in_90, in_106, in_122, in_11, in_27, in_43, in_59, in_75, in_91, in_107, in_123, in_12, in_28, in_44, in_60, in_76, in_92, in_108, in_124, in_13, in_29, in_45, in_61, in_77, in_93, in_109, in_125, in_14, in_30, in_46, in_62, in_78, in_94, in_110, in_126, in_15, in_31, in_47, in_63, in_79, in_95, in_111, in_127, in_16, in_32, in_48, in_64, in_80, in_96, in_112, in_128, in_17, in_33, in_49, in_65, in_81, in_97, in_113, in_129, in_2, in_3, in_4, in_5, in_6, in_7, in_8, in_9, in_18, in_19, in_20, in_21, in_22, in_23, in_24, in_25, in_34, in_35, in_36, in_37, in_38, in_39, in_40, in_41, in_50, in_51, in_52, in_53, in_54, in_55, in_56, in_57, in_66, in_67, in_68, in_69, in_70, in_71, in_72, in_73, in_82, in_83, in_84, in_85, in_86, in_87, in_88, in_89, in_98, in_99, in_100, in_101, in_102, in_103, in_104, in_105, in_114, in_115, in_116, in_117, in_118, in_119, in_120, in_121
  screen_map screen_map_1 (
    .Select(Current_location), .in_1(Clock_input));  // open: out_11, out_27, out_43, out_59, out_75, out_91, out_107, out_123, out_12, out_28, out_44, out_60, out_76, out_92, out_108, out_124, out_13, out_29, out_45, out_61, out_77, out_93, out_109, out_125, out_14, out_30, out_46, out_62, out_78, out_94, out_110, out_126, out_15, out_31, out_47, out_63, out_79, out_95, out_111, out_127, out_16, out_32, out_48, out_64, out_80, out_96, out_112, out_128, out_17, out_33, out_49, out_65, out_81, out_97, out_113, out_129, out_18, out_34, out_50, out_66, out_82, out_98, out_114, out_130, out_3, out_19, out_35, out_51, out_67, out_83, out_99, out_115, out_4, out_20, out_36, out_52, out_68, out_84, out_100, out_116, out_5, out_21, out_37, out_53, out_69, out_85, out_101, out_117, out_6, out_22, out_38, out_54, out_70, out_86, out_102, out_118, out_7, out_23, out_39, out_55, out_71, out_87, out_103, out_119, out_8, out_24, out_40, out_56, out_72, out_88, out_104, out_120, out_9, out_25, out_41, out_57, out_73, out_89, out_105, out_121, out_10, out_26, out_42, out_58, out_74, out_90, out_106, out_122
  Multiplexer #(.width(12)) multiplexer_1 (
    .in0(register_1_q), .in1(in_1), .out(multiplexer_1_out), .sel(in_2));  // open: en
  movement_check movement_check_1 (
    .New_location(New_location), .Overflow_flag(movement_check_1_overflow_flag),
    .Current_position(multiplexer_1_out), .Movement_direction(out_3));
  buf or_1 (or_1_out, movement_check_1_overflow_flag);  // OR_Gate
  not not_1 (not_1_out, or_1_out);
  and and_1 (and_1_out, not_1_out, Clock_input);
  Register #(.width(12)) register_1 (.D(New_location), .Q(register_1_q), .clk(and_1_out));  // open: en, clr

  // Other names for the same wires on the sheet: Direction_input[2:0] = out_3

  // Notes on the sheet:
  //   contents of rom_1 (hex, n*v repeats v):
  //   97*0 7 0 0 5 14*0 6 0 0 0 4
endmodule

module screen_map (
  input  in_1,
  input  [11:0] Select,
  output [31:0] out_3,
  output [31:0] out_4,
  output [31:0] out_5,
  output [31:0] out_6,
  output [31:0] out_7,
  output [31:0] out_8,
  output [31:0] out_9,
  output [31:0] out_10,
  output [31:0] out_11,
  output [31:0] out_12,
  output [31:0] out_13,
  output [31:0] out_14,
  output [31:0] out_15,
  output [31:0] out_16,
  output [31:0] out_17,
  output [31:0] out_18,
  output [31:0] out_19,
  output [31:0] out_20,
  output [31:0] out_21,
  output [31:0] out_22,
  output [31:0] out_23,
  output [31:0] out_24,
  output [31:0] out_25,
  output [31:0] out_26,
  output [31:0] out_27,
  output [31:0] out_28,
  output [31:0] out_29,
  output [31:0] out_30,
  output [31:0] out_31,
  output [31:0] out_32,
  output [31:0] out_33,
  output [31:0] out_34,
  output [31:0] out_35,
  output [31:0] out_36,
  output [31:0] out_37,
  output [31:0] out_38,
  output [31:0] out_39,
  output [31:0] out_40,
  output [31:0] out_41,
  output [31:0] out_42,
  output [31:0] out_43,
  output [31:0] out_44,
  output [31:0] out_45,
  output [31:0] out_46,
  output [31:0] out_47,
  output [31:0] out_48,
  output [31:0] out_49,
  output [31:0] out_50,
  output [31:0] out_51,
  output [31:0] out_52,
  output [31:0] out_53,
  output [31:0] out_54,
  output [31:0] out_55,
  output [31:0] out_56,
  output [31:0] out_57,
  output [31:0] out_58,
  output [31:0] out_59,
  output [31:0] out_60,
  output [31:0] out_61,
  output [31:0] out_62,
  output [31:0] out_63,
  output [31:0] out_64,
  output [31:0] out_65,
  output [31:0] out_66,
  output [31:0] out_67,
  output [31:0] out_68,
  output [31:0] out_69,
  output [31:0] out_70,
  output [31:0] out_71,
  output [31:0] out_72,
  output [31:0] out_73,
  output [31:0] out_74,
  output [31:0] out_75,
  output [31:0] out_76,
  output [31:0] out_77,
  output [31:0] out_78,
  output [31:0] out_79,
  output [31:0] out_80,
  output [31:0] out_81,
  output [31:0] out_82,
  output [31:0] out_83,
  output [31:0] out_84,
  output [31:0] out_85,
  output [31:0] out_86,
  output [31:0] out_87,
  output [31:0] out_88,
  output [31:0] out_89,
  output [31:0] out_90,
  output [31:0] out_91,
  output [31:0] out_92,
  output [31:0] out_93,
  output [31:0] out_94,
  output [31:0] out_95,
  output [31:0] out_96,
  output [31:0] out_97,
  output [31:0] out_98,
  output [31:0] out_99,
  output [31:0] out_100,
  output [31:0] out_101,
  output [31:0] out_102,
  output [31:0] out_103,
  output [31:0] out_104,
  output [31:0] out_105,
  output [31:0] out_106,
  output [31:0] out_107,
  output [31:0] out_108,
  output [31:0] out_109,
  output [31:0] out_110,
  output [31:0] out_111,
  output [31:0] out_112,
  output [31:0] out_113,
  output [31:0] out_114,
  output [31:0] out_115,
  output [31:0] out_116,
  output [31:0] out_117,
  output [31:0] out_118,
  output [31:0] out_119,
  output [31:0] out_120,
  output [31:0] out_121,
  output [31:0] out_122,
  output [31:0] out_123,
  output [31:0] out_124,
  output [31:0] out_125,
  output [31:0] out_126,
  output [31:0] out_127,
  output [31:0] out_128,
  output [31:0] out_129,
  output [31:0] out_130
);

  wire [31:0] mask_low, mask_up;

  row_map row_map_1 (.Select(Select[11:6]), .out_2(mask_low), .out_3(mask_up));
  bit_mask bit_mask_1 (.Masked(mask_low[31]), .Out1(out_11), .Select(Select[5:0]), .Out2(out_12), .Enabled(in_1));
  bit_mask bit_mask_2 (.Masked(mask_low[30]), .Out1(out_27), .Select(Select[5:0]), .Out2(out_28), .Enabled(in_1));
  bit_mask bit_mask_3 (.Masked(mask_low[29]), .Out1(out_43), .Select(Select[5:0]), .Out2(out_44), .Enabled(in_1));
  bit_mask bit_mask_4 (.Masked(mask_low[28]), .Out1(out_59), .Select(Select[5:0]), .Out2(out_60), .Enabled(in_1));
  bit_mask bit_mask_5 (.Masked(mask_low[27]), .Out1(out_75), .Select(Select[5:0]), .Out2(out_76), .Enabled(in_1));
  bit_mask bit_mask_6 (.Masked(mask_low[26]), .Out1(out_91), .Select(Select[5:0]), .Out2(out_92), .Enabled(in_1));
  bit_mask bit_mask_7 (.Masked(mask_low[25]), .Out1(out_107), .Select(Select[5:0]), .Out2(out_108), .Enabled(in_1));
  bit_mask bit_mask_8 (.Masked(mask_low[24]), .Out1(out_123), .Select(Select[5:0]), .Out2(out_124), .Enabled(in_1));
  bit_mask bit_mask_9 (.Masked(mask_low[23]), .Out1(out_13), .Select(Select[5:0]), .Out2(out_14), .Enabled(in_1));
  bit_mask bit_mask_10 (.Masked(mask_low[22]), .Out1(out_29), .Select(Select[5:0]), .Out2(out_30), .Enabled(in_1));
  bit_mask bit_mask_11 (.Masked(mask_low[21]), .Out1(out_45), .Select(Select[5:0]), .Out2(out_46), .Enabled(in_1));
  bit_mask bit_mask_12 (.Masked(mask_low[20]), .Out1(out_61), .Select(Select[5:0]), .Out2(out_62), .Enabled(in_1));
  bit_mask bit_mask_13 (.Masked(mask_low[19]), .Out1(out_77), .Select(Select[5:0]), .Out2(out_78), .Enabled(in_1));
  bit_mask bit_mask_14 (.Masked(mask_low[18]), .Out1(out_93), .Select(Select[5:0]), .Out2(out_94), .Enabled(in_1));
  bit_mask bit_mask_15 (.Masked(mask_low[17]), .Out1(out_109), .Select(Select[5:0]), .Out2(out_110), .Enabled(in_1));
  bit_mask bit_mask_16 (.Masked(mask_low[16]), .Out1(out_125), .Select(Select[5:0]), .Out2(out_126), .Enabled(in_1));
  bit_mask bit_mask_17 (.Masked(mask_low[15]), .Out1(out_15), .Select(Select[5:0]), .Out2(out_16), .Enabled(in_1));
  bit_mask bit_mask_18 (.Masked(mask_low[14]), .Out1(out_31), .Select(Select[5:0]), .Out2(out_32), .Enabled(in_1));
  bit_mask bit_mask_19 (.Masked(mask_low[13]), .Out1(out_47), .Select(Select[5:0]), .Out2(out_48), .Enabled(in_1));
  bit_mask bit_mask_20 (.Masked(mask_low[12]), .Out1(out_63), .Select(Select[5:0]), .Out2(out_64), .Enabled(in_1));
  bit_mask bit_mask_21 (.Masked(mask_low[11]), .Out1(out_79), .Select(Select[5:0]), .Out2(out_80), .Enabled(in_1));
  bit_mask bit_mask_22 (.Masked(mask_low[10]), .Out1(out_95), .Select(Select[5:0]), .Out2(out_96), .Enabled(in_1));
  bit_mask bit_mask_23 (.Masked(mask_low[9]), .Out1(out_111), .Select(Select[5:0]), .Out2(out_112), .Enabled(in_1));
  bit_mask bit_mask_24 (.Masked(mask_low[8]), .Out1(out_127), .Select(Select[5:0]), .Out2(out_128), .Enabled(in_1));
  bit_mask bit_mask_25 (.Masked(mask_low[7]), .Out1(out_17), .Select(Select[5:0]), .Out2(out_18), .Enabled(in_1));
  bit_mask bit_mask_26 (.Masked(mask_low[6]), .Out1(out_33), .Select(Select[5:0]), .Out2(out_34), .Enabled(in_1));
  bit_mask bit_mask_27 (.Masked(mask_low[5]), .Out1(out_49), .Select(Select[5:0]), .Out2(out_50), .Enabled(in_1));
  bit_mask bit_mask_28 (.Masked(mask_low[4]), .Out1(out_65), .Select(Select[5:0]), .Out2(out_66), .Enabled(in_1));
  bit_mask bit_mask_29 (.Masked(mask_low[3]), .Out1(out_81), .Select(Select[5:0]), .Out2(out_82), .Enabled(in_1));
  bit_mask bit_mask_30 (.Masked(mask_low[2]), .Out1(out_97), .Select(Select[5:0]), .Out2(out_98), .Enabled(in_1));
  bit_mask bit_mask_31 (.Masked(mask_low[1]), .Out1(out_113), .Select(Select[5:0]), .Out2(out_114), .Enabled(in_1));
  bit_mask bit_mask_32 (.Masked(mask_low[0]), .Out1(out_129), .Select(Select[5:0]), .Out2(out_130), .Enabled(in_1));
  bit_mask bit_mask_33 (.Masked(mask_up[31]), .Out1(out_3), .Select(Select[5:0]), .Out2(out_4), .Enabled(in_1));
  bit_mask bit_mask_34 (.Masked(mask_up[30]), .Out1(out_19), .Select(Select[5:0]), .Out2(out_20), .Enabled(in_1));
  bit_mask bit_mask_35 (.Masked(mask_up[29]), .Out1(out_35), .Select(Select[5:0]), .Out2(out_36), .Enabled(in_1));
  bit_mask bit_mask_36 (.Masked(mask_up[28]), .Out1(out_51), .Select(Select[5:0]), .Out2(out_52), .Enabled(in_1));
  bit_mask bit_mask_37 (.Masked(mask_up[27]), .Out1(out_67), .Select(Select[5:0]), .Out2(out_68), .Enabled(in_1));
  bit_mask bit_mask_38 (.Masked(mask_up[26]), .Out1(out_83), .Select(Select[5:0]), .Out2(out_84), .Enabled(in_1));
  bit_mask bit_mask_39 (.Masked(mask_up[25]), .Out1(out_99), .Select(Select[5:0]), .Out2(out_100), .Enabled(in_1));
  bit_mask bit_mask_40 (.Masked(mask_up[24]), .Out1(out_115), .Select(Select[5:0]), .Out2(out_116), .Enabled(in_1));
  bit_mask bit_mask_41 (.Masked(mask_up[23]), .Out1(out_5), .Select(Select[5:0]), .Out2(out_6), .Enabled(in_1));
  bit_mask bit_mask_42 (.Masked(mask_up[22]), .Out1(out_21), .Select(Select[5:0]), .Out2(out_22), .Enabled(in_1));
  bit_mask bit_mask_43 (.Masked(mask_up[21]), .Out1(out_37), .Select(Select[5:0]), .Out2(out_38), .Enabled(in_1));
  bit_mask bit_mask_44 (.Masked(mask_up[20]), .Out1(out_53), .Select(Select[5:0]), .Out2(out_54), .Enabled(in_1));
  bit_mask bit_mask_45 (.Masked(mask_up[19]), .Out1(out_69), .Select(Select[5:0]), .Out2(out_70), .Enabled(in_1));
  bit_mask bit_mask_46 (.Masked(mask_up[18]), .Out1(out_85), .Select(Select[5:0]), .Out2(out_86), .Enabled(in_1));
  bit_mask bit_mask_47 (.Masked(mask_up[17]), .Out1(out_101), .Select(Select[5:0]), .Out2(out_102), .Enabled(in_1));
  bit_mask bit_mask_48 (.Masked(mask_up[16]), .Out1(out_117), .Select(Select[5:0]), .Out2(out_118), .Enabled(in_1));
  bit_mask bit_mask_49 (.Masked(mask_up[15]), .Out1(out_7), .Select(Select[5:0]), .Out2(out_8), .Enabled(in_1));
  bit_mask bit_mask_50 (.Masked(mask_up[14]), .Out1(out_23), .Select(Select[5:0]), .Out2(out_24), .Enabled(in_1));
  bit_mask bit_mask_51 (.Masked(mask_up[13]), .Out1(out_39), .Select(Select[5:0]), .Out2(out_40), .Enabled(in_1));
  bit_mask bit_mask_52 (.Masked(mask_up[12]), .Out1(out_55), .Select(Select[5:0]), .Out2(out_56), .Enabled(in_1));
  bit_mask bit_mask_53 (.Masked(mask_up[11]), .Out1(out_71), .Select(Select[5:0]), .Out2(out_72), .Enabled(in_1));
  bit_mask bit_mask_54 (.Masked(mask_up[10]), .Out1(out_87), .Select(Select[5:0]), .Out2(out_88), .Enabled(in_1));
  bit_mask bit_mask_55 (.Masked(mask_up[9]), .Out1(out_103), .Select(Select[5:0]), .Out2(out_104), .Enabled(in_1));
  bit_mask bit_mask_56 (.Masked(mask_up[8]), .Out1(out_119), .Select(Select[5:0]), .Out2(out_120), .Enabled(in_1));
  bit_mask bit_mask_57 (.Masked(mask_up[7]), .Out1(out_9), .Select(Select[5:0]), .Out2(out_10), .Enabled(in_1));
  bit_mask bit_mask_58 (.Masked(mask_up[6]), .Out1(out_25), .Select(Select[5:0]), .Out2(out_26), .Enabled(in_1));
  bit_mask bit_mask_59 (.Masked(mask_up[5]), .Out1(out_41), .Select(Select[5:0]), .Out2(out_42), .Enabled(in_1));
  bit_mask bit_mask_60 (.Masked(mask_up[4]), .Out1(out_57), .Select(Select[5:0]), .Out2(out_58), .Enabled(in_1));
  bit_mask bit_mask_61 (.Masked(mask_up[3]), .Out1(out_73), .Select(Select[5:0]), .Out2(out_74), .Enabled(in_1));
  bit_mask bit_mask_62 (.Masked(mask_up[2]), .Out1(out_89), .Select(Select[5:0]), .Out2(out_90), .Enabled(in_1));
  bit_mask bit_mask_63 (.Masked(mask_up[1]), .Out1(out_105), .Select(Select[5:0]), .Out2(out_106), .Enabled(in_1));
  bit_mask bit_mask_64 (.Masked(mask_up[0]), .Out1(out_121), .Select(Select[5:0]), .Out2(out_122), .Enabled(in_1));

  // Other names for the same wires on the sheet: On = in_1; sel_low[5:0] = Select[5:0]
endmodule

module row_map (
  input  [5:0] Select,
  output [31:0] out_2,
  output [31:0] out_3
);

  wire [4:0] not_1_out;
  wire [31:0] and_1_out, and_2_out, column_switch, not_2_out;

  assign column_switch = {{31{Select[5]}}, Select[5]};  // Bit_Extender bit_extender_1
  assign not_1_out = ~Select[4:0];  // NOT_Gate not_1, 5 bits wide
  assign and_1_out = 32'h1 & not_2_out;  // AND_Gate and_1, 32 bits wide
  assign not_2_out = ~column_switch;  // NOT_Gate not_2, 32 bits wide
  assign and_2_out = 32'h1 & column_switch;  // AND_Gate and_2, 32 bits wide
  Shifter #(.width(32)) shifter_1 (.in(and_1_out), .\dist (not_1_out), .out(out_2));
  Shifter #(.width(32)) shifter_2 (.in(and_2_out), .\dist (not_1_out), .out(out_3));
endmodule

module bit_mask (
  input  Enabled,
  input  [5:0] Select,
  input  Masked,
  output [31:0] Out1,
  output [31:0] Out2
);

  wire and_1_out;
  wire [31:0] bit_extender_1_out, row_map_1_out_2, row_map_1_out_3;

  and and_1 (and_1_out, Enabled, Masked);
  assign Out1 = bit_extender_1_out & row_map_1_out_2;  // AND_Gate and_2, 32 bits wide
  assign bit_extender_1_out = {{31{and_1_out}}, and_1_out};  // Bit_Extender bit_extender_1
  assign Out2 = bit_extender_1_out & row_map_1_out_3;  // AND_Gate and_3, 32 bits wide
  row_map row_map_1 (.Select(Select), .out_2(row_map_1_out_2), .out_3(row_map_1_out_3));
endmodule
