// Logisim project addressDirection.circ as structural Verilog: 1 circuit, main circuit addressDirection
module addressDirection (
  input  [1:0] Direction,
  input  [5:0] Address,
  output [5:0] Address_of_room_in_direction
);

  wire [5:0] adder_1_out, adder_2_out, demultiplexer_1_out0, demultiplexer_1_out1, demultiplexer_1_out2,
       demultiplexer_1_out3, subtractor_1_out, subtractor_2_out;

  Demultiplexer #(.select(2), .width(6), .enable("false")) demultiplexer_1 (
    .out0(demultiplexer_1_out0), .out1(demultiplexer_1_out1), .out2(demultiplexer_1_out2),
    .out3(demultiplexer_1_out3), .in(Address), .sel(Direction));
  Subtractor #(.width(6)) subtractor_1 (
    .a(demultiplexer_1_out0), .b(6'b001000), .out(subtractor_1_out));  // open: bin, bout
  Adder #(.width(6)) adder_1 (.a(demultiplexer_1_out1), .b(6'b000001), .out(adder_1_out));  // open: cin, cout
  Adder #(.width(6)) adder_2 (.a(demultiplexer_1_out2), .b(6'b001000), .out(adder_2_out));  // open: cin, cout
  Subtractor #(.width(6)) subtractor_2 (
    .a(demultiplexer_1_out3), .b(6'b000001), .out(subtractor_2_out));  // open: bin, bout
  Multiplexer #(.select(2), .width(6), .enable("false")) multiplexer_1 (
    .in0(subtractor_1_out), .in1(adder_1_out), .in2(adder_2_out), .in3(subtractor_2_out),
    .out(Address_of_room_in_direction), .sel(Direction));
endmodule
