// Logisim project doorChooser.circ as structural Verilog: 1 circuit, main circuit doorChooser
module doorChooser (
  input  [5:0] Addr,
  input  CLK,
  output [3:0] Choosen_Rooms
);

  wire comparator_1_lt, comparator_2_gt, comparator_3_gt, comparator_4_lt;
  wire [3:0] random_1_out;
  wire [5:0] divider_1_rem, divider_2_rem;

  Divider #(.width(6)) divider_1 (.a(Addr), .b(6'b001000), .rem(divider_1_rem));  // open: out, upper
  Divider #(.width(6)) divider_2 (.a(Addr), .b(6'b001000), .rem(divider_2_rem));  // open: out, upper
  Comparator #(.width(6), .mode("unsigned")) comparator_1 (
    .a(6'b001000), .b(Addr), .lt(comparator_1_lt));  // open: gt, eq
  Comparator #(.width(6), .mode("unsigned")) comparator_2 (
    .a(6'b000111), .b(divider_1_rem), .gt(comparator_2_gt));  // open: eq, lt
  Comparator #(.width(6), .mode("unsigned")) comparator_3 (
    .a(6'b111000), .b(Addr), .gt(comparator_3_gt));  // open: eq, lt
  Comparator #(.width(6), .mode("unsigned")) comparator_4 (
    .a({6{1'b0}}), .b(divider_2_rem), .lt(comparator_4_lt));  // open: gt, eq
  Random #(.width(4)) random_1 (.clk(CLK), .out(random_1_out));  // open: next, clr
  and and_1 (Choosen_Rooms[3], comparator_1_lt, random_1_out[3]);
  and and_2 (Choosen_Rooms[2], comparator_2_gt, random_1_out[2]);
  and and_3 (Choosen_Rooms[1], comparator_3_gt, random_1_out[1]);
  and and_4 (Choosen_Rooms[0], comparator_4_lt, random_1_out[0]);

  // Notes on the sheet:
  //   Up
  //   Right
  //   Down
  //   Left
endmodule
