// Logisim project doorDataGenerator.circ as structural Verilog: 1 circuit, main circuit doorDataGenerator
module doorDataGenerator (
  input  Input,
  input  [1:0] Direction,
  output [3:0] Doors,
  output [3:0] Doors__Inversed
);

  wire [1:1] not_1_out;

  Shifter #(.width(4), .shift("lr")) shifter_1 (.in({Input, 3'b000}), .\dist (Direction), .out(Doors));
  Shifter #(.width(4), .shift("lr")) shifter_2 (
    .in({Input, 3'b000}), .\dist ({not_1_out[1], Direction[0]}), .out(Doors__Inversed));
  not not_1 (not_1_out[1], Direction[1]);
endmodule
