// Logisim project memoryReadColumnControl.circ as structural Verilog: 1 circuit, main circuit memoryReadColumnControl
module memoryReadColumnControl (
  input  [2:0] in_1,
  output out_2,
  output out_3,
  output out_4,
  output out_5,
  output out_6,
  output out_7,
  output out_8,
  output out_9
);

  and and_1 (out_2, ~in_1[0], ~in_1[1], ~in_1[2]);  // AND_Gate
  and and_2 (out_3, in_1[0], ~in_1[1], ~in_1[2]);  // AND_Gate
  and and_3 (out_4, ~in_1[0], in_1[1], ~in_1[2]);  // AND_Gate
  and and_4 (out_5, in_1[0], in_1[1], ~in_1[2]);  // AND_Gate
  and and_5 (out_6, ~in_1[0], ~in_1[1], in_1[2]);  // AND_Gate
  and and_6 (out_7, in_1[0], ~in_1[1], in_1[2]);  // AND_Gate
  and and_7 (out_8, ~in_1[0], in_1[1], in_1[2]);  // AND_Gate
  and and_8 (out_9, in_1[0], in_1[1], in_1[2]);
endmodule
