// Logisim project memoryReadControl.circ as structural Verilog: 1 circuit, main circuit memoryReadControl
module memoryReadControl (
  input  CLK,
  input  Write,
  input  [31:0] Data,
  output [31:0] out_4,
  output [5:0] A,
  output [31:0] out_6,
  output [31:0] out_7,
  output [31:0] out_8,
  output [31:0] out_9,
  output [31:0] out_10,
  output [31:0] out_11,
  output [31:0] out_12
);

  wire and_1_out;
  wire [31:0] demultiplexer_1_out0, demultiplexer_1_out1, demultiplexer_1_out2, demultiplexer_1_out3,
       demultiplexer_1_out4, demultiplexer_1_out5, demultiplexer_1_out6, demultiplexer_1_out7;

  and and_1 (and_1_out, CLK, Write);
  Counter #(.width(3), .max('h7), .trigger("falling")) counter_1 (
    .Q(A[5:3]), .clk(and_1_out));  // open: load, D, count, carry, clr
  Demultiplexer #(.select(3), .width(32), .enable("false")) demultiplexer_1 (
    .out0(demultiplexer_1_out0), .out1(demultiplexer_1_out1), .out2(demultiplexer_1_out2),
    .out3(demultiplexer_1_out3), .out4(demultiplexer_1_out4), .out5(demultiplexer_1_out5),
    .out6(demultiplexer_1_out6), .out7(demultiplexer_1_out7), .in(Data), .sel(A[5:3]));
  _8x32bit_Register u_8x32bit_register_1 (
    .Inputs(demultiplexer_1_out0), .in_2(demultiplexer_1_out1), .in_3(demultiplexer_1_out2),
    .in_4(demultiplexer_1_out3), .in_5(demultiplexer_1_out4), .in_6(demultiplexer_1_out5), .CLK(and_1_out),
    .Select(A[5:3]), .in_7(demultiplexer_1_out6), .in_8(demultiplexer_1_out7), .out_12(out_4),
    .out_13(out_6), .out_14(out_7), .out_15(out_8), .out_16(out_9), .out_17(out_10), .out_18(out_11),
    .out_19(out_12));  // open: RST

  assign A[2:0] = 3'b000;

  // Notes on the sheet:
  //   LED Output
endmodule
