// Logisim project memoryRowDataConnector.circ as structural Verilog: 1 circuit, main circuit MemoryRowDataConnector
module MemoryRowDataConnector (
  input  [3:0] in_1,
  input  [3:0] in_2,
  input  [3:0] in_3,
  input  [3:0] in_4,
  input  [3:0] in_5,
  input  [3:0] in_6,
  input  [3:0] in_7,
  input  [3:0] in_8,
  input  [3:0] in_9,
  input  [3:0] in_10,
  input  [3:0] in_11,
  input  [3:0] in_12,
  input  [3:0] in_13,
  input  [3:0] in_14,
  input  [3:0] in_15,
  input  [3:0] in_16,
  input  in_17,
  input  in_18,
  input  in_19,
  input  in_20,
  input  in_21,
  input  in_22,
  input  in_23,
  input  in_24,
  output [3:0] out_25,
  output [3:0] out_26,
  output [3:0] out_27,
  output [3:0] out_28,
  output [3:0] Output,
  output [3:0] out_30,
  output [3:0] out_31,
  output [3:0] out_32
);

  Multiplexer #(.width(4), .enable("false")) multiplexer_1 (.in0(in_7), .in1(in_15), .out(out_31), .sel(in_23));
  Multiplexer #(.width(4), .enable("false")) multiplexer_2 (.in0(in_8), .in1(in_16), .out(out_32), .sel(in_24));
  Multiplexer #(.width(4), .enable("false")) multiplexer_3 (.in0(in_5), .in1(in_13), .out(Output), .sel(in_21));
  Multiplexer #(.width(4), .enable("false")) multiplexer_4 (.in0(in_6), .in1(in_14), .out(out_30), .sel(in_22));
  Multiplexer #(.width(4), .enable("false")) multiplexer_5 (.in0(in_3), .in1(in_11), .out(out_27), .sel(in_19));
  Multiplexer #(.width(4), .enable("false")) multiplexer_6 (.in0(in_4), .in1(in_12), .out(out_28), .sel(in_20));
  Multiplexer #(.width(4), .enable("false")) multiplexer_7 (.in0(in_1), .in1(in_9), .out(out_25), .sel(in_17));
  Multiplexer #(.width(4), .enable("false")) multiplexer_8 (.in0(in_2), .in1(in_10), .out(out_26), .sel(in_18));

  // Notes on the sheet:
  //   Data from RAM
  //   New Data
endmodule
