// Logisim project roomAddressInterface.circ as structural Verilog: 1 circuit, main circuit main
module main (
  input  Row_minus_minus,
  input  Row_plus_plus,
  input  Column_minus_minus,
  input  Column_plus_plus,
  output [7:0] Room_Select_Display_Output,
  output [7:0] out_6,
  output [7:0] out_7,
  output [7:0] out_8,
  output [7:0] out_9,
  output [7:0] out_10,
  output [7:0] out_11,
  output [7:0] out_12,
  output [5:0] Room_Address
);

  wire or_1_out, or_2_out;
  wire [7:0] shifter_1_out;

  Counter #(.width(3), .max('h7)) counter_1 (
    .load(Row_minus_minus), .Q(Room_Address[5:3]), .clk(or_1_out));  // open: D, count, carry, clr
  or or_1 (or_1_out, Row_minus_minus, Row_plus_plus);
  Counter #(.width(3), .max('h7)) counter_2 (
    .load(Column_minus_minus), .Q(Room_Address[2:0]), .clk(or_2_out));  // open: D, count, carry, clr
  or or_2 (or_2_out, Column_minus_minus, Column_plus_plus);
  Shifter #(.shift("lr")) shifter_1 (.in(8'h80), .\dist (Room_Address[2:0]), .out(shifter_1_out));
  Demultiplexer #(.select(3), .width(8), .disabled(0), .enable("false")) demultiplexer_1 (
    .out0(Room_Select_Display_Output), .out1(out_6), .out2(out_7), .out3(out_8), .out4(out_9), .out5(out_10),
    .out6(out_11), .out7(out_12), .in(shifter_1_out), .sel(Room_Address[5:3]));
endmodule
