// Logisim project roomLimit.circ as structural Verilog: 1 circuit, main circuit main
module main (
  input  CLK,
  input  _0,
  input  [7:0] Room_Limit,
  output [7:0] Room_Counter,
  output Room_Limit_Flag
);

  wire comparator_1_eq, comparator_1_gt;

  Counter counter_1 (.Q(Room_Counter), .clk(CLK), .clr(_0));  // open: load, D, count, carry
  Comparator #(.mode("unsigned")) comparator_1 (
    .a(Room_Counter), .b(Room_Limit), .gt(comparator_1_gt), .eq(comparator_1_eq));  // open: lt
  or or_1 (Room_Limit_Flag, comparator_1_gt, comparator_1_eq);
endmodule
