// Logisim project roomLimitInterface.circ as structural Verilog: 1 circuit, main circuit roomLimitInterface
module roomLimitInterface (
  input  plus_10,
  input  plus_1,
  input  minus_10,
  input  minus_1,
  output [7:0] Data_Output,
  output [15:0] _7_Segment_Output
);

  wire and_1_out, and_2_out, and_3_out, and_4_out, and_5_out, and_6_out, and_7_out, and_8_out,
       comparator_1_eq, comparator_1_gt, comparator_1_lt, comparator_2_eq, comparator_2_gt, comparator_2_lt,
       comparator_3_eq, comparator_3_gt, comparator_3_lt, comparator_4_eq, comparator_4_gt, comparator_4_lt,
       or_1_out, or_2_out, or_3_out, or_4_out, or_5_out;
  wire [7:0] adder_1_out, adder_2_out, controlled_buffer_1_out, subtractor_1_out, subtractor_2_out;

  Comparator comparator_1 (
    .a(Data_Output), .b(8'h36), .gt(comparator_1_gt), .eq(comparator_1_eq), .lt(comparator_1_lt));
  or or_1 (or_1_out, comparator_1_eq, comparator_1_lt);
  Adder adder_1 (.a(Data_Output), .b(8'ha), .out(adder_1_out));  // open: cin, cout
  Comparator comparator_2 (
    .a(Data_Output), .b(8'h3f), .gt(comparator_2_gt), .eq(comparator_2_eq), .lt(comparator_2_lt));
  or or_2 (or_2_out, comparator_2_eq, comparator_2_lt);
  Adder adder_2 (.a(Data_Output), .b(8'h1), .out(adder_2_out));  // open: cin, cout
  Comparator comparator_3 (.a(Data_Output), .b(8'h9), .gt(comparator_3_gt), .eq(comparator_3_eq), .lt(comparator_3_lt));
  or or_3 (or_3_out, comparator_3_eq, comparator_3_lt);
  Subtractor subtractor_1 (.a(Data_Output), .b(8'ha), .out(subtractor_1_out));  // open: bin, bout
  Comparator comparator_4 (
    .a(Data_Output), .b({8{1'b0}}), .gt(comparator_4_gt), .eq(comparator_4_eq), .lt(comparator_4_lt));
  or or_4 (or_4_out, comparator_4_eq, comparator_4_lt);
  Subtractor subtractor_2 (.a(Data_Output), .b(8'h1), .out(subtractor_2_out));  // open: bin, bout
  and and_1 (and_1_out, comparator_1_gt, plus_10);
  and and_2 (and_2_out, or_1_out, plus_10);
  assign controlled_buffer_1_out = and_2_out ? adder_1_out : 8'bz;  // Controlled_Buffer controlled_buffer_1
  and and_3 (and_3_out, comparator_2_gt, plus_1);
  and and_4 (and_4_out, or_2_out, plus_1);
  assign controlled_buffer_1_out = and_4_out ? adder_2_out : 8'bz;  // Controlled_Buffer controlled_buffer_2
  and and_5 (and_5_out, comparator_3_gt, minus_10);
  and and_6 (and_6_out, or_3_out, minus_10);
  assign controlled_buffer_1_out = and_1_out ? 8'h40 : 8'bz;  // Controlled_Buffer controlled_buffer_3
  assign controlled_buffer_1_out = and_3_out ? 8'h40 : 8'bz;  // Controlled_Buffer controlled_buffer_4
  assign controlled_buffer_1_out = and_6_out ? {8{1'b0}} : 8'bz;  // Controlled_Buffer controlled_buffer_5
  assign controlled_buffer_1_out = and_5_out ? subtractor_1_out : 8'bz;  // Controlled_Buffer controlled_buffer_6
  and and_7 (and_7_out, comparator_4_gt, minus_1);
  and and_8 (and_8_out, or_4_out, minus_1);
  assign controlled_buffer_1_out = and_7_out ? subtractor_2_out : 8'bz;  // Controlled_Buffer controlled_buffer_7
  assign controlled_buffer_1_out = and_8_out ? {8{1'b0}} : 8'bz;  // Controlled_Buffer controlled_buffer_8
  Register #(.trigger("falling")) register_1 (
    .D(controlled_buffer_1_out), .Q(Data_Output), .clk(or_5_out));  // open: en, clr
  or or_5 (or_5_out, minus_1, minus_10, plus_1, plus_10);
  ROM #(.dataWidth(16)) rom_1 (.addr(Data_Output), .data(_7_Segment_Output));  // open: sel

  // Notes on the sheet:
  //   contents of rom_1 (hex, n*v repeats v):
  //   7e7e 7e12 7ebc 7eb6 7ed2 7ee6 7eef 7e32 7efe 7ef7 127e 1212 12bc 12b6 12d2 12e6 12ef 1232 12fe 12f7
  //   bc7e bc12 bcbc bcb6 bcd2 bce6 bcef bc32 bcfe bcf7 b67e b612 b6bc b6b6 b6d2 b6e6 b6ef b632 b6fe b6f7
  //   d27e d212 d2bc d2b6 d2d2 d2e6 d2ef d232 d2fe d2f7 e67e e612 e6bc e6b6 e6d2 e6e6 e6ef e632 e6fe e6f7
  //   ef7e ef12 efbc efb6 efd2
endmodule
