// Logisim project roomMemory.circ as structural Verilog: 1 circuit, main circuit roomMemory
module roomMemory (
  input  CLK,
  input  Write,
  input  Reset,
  input  [3:0] D,
  input  [5:0] A,
  output [31:0] out_6,
  output [3:0] out_7
);

  wire [3:0] demultiplexer_1_out0, demultiplexer_1_out1, demultiplexer_1_out2, demultiplexer_1_out3,
       demultiplexer_1_out4, demultiplexer_1_out5, demultiplexer_1_out6, demultiplexer_1_out7;
  wire [7:0] shifter_1_out;
  wire [31:0] memoryrowdataconnector_1_out_32;

  Demultiplexer #(.select(3), .width(4), .enable("false")) demultiplexer_1 (
    .out0(demultiplexer_1_out0), .out1(demultiplexer_1_out1), .out2(demultiplexer_1_out2),
    .out3(demultiplexer_1_out3), .out4(demultiplexer_1_out4), .out5(demultiplexer_1_out5),
    .out6(demultiplexer_1_out6), .out7(demultiplexer_1_out7), .in(D), .sel(A[2:0]));
  MemoryRowDataConnector memoryrowdataconnector_1 (
    .in_1(out_6[31:28]), .in_2(out_6[27:24]), .in_3(out_6[23:20]), .in_4(out_6[19:16]), .in_5(out_6[15:12]),
    .in_6(out_6[11:8]), .in_7(out_6[7:4]), .in_8(out_6[3:0]), .in_9(demultiplexer_1_out0),
    .in_10(demultiplexer_1_out1), .in_11(demultiplexer_1_out2), .in_12(demultiplexer_1_out3),
    .in_13(demultiplexer_1_out4), .in_14(demultiplexer_1_out5), .in_15(demultiplexer_1_out6),
    .in_16(demultiplexer_1_out7), .in_17(shifter_1_out[7]), .out_25(memoryrowdataconnector_1_out_32[31:28]),
    .out_26(memoryrowdataconnector_1_out_32[27:24]), .out_27(memoryrowdataconnector_1_out_32[23:20]),
    .out_28(memoryrowdataconnector_1_out_32[19:16]), .Output(memoryrowdataconnector_1_out_32[15:12]),
    .out_30(memoryrowdataconnector_1_out_32[11:8]), .out_31(memoryrowdataconnector_1_out_32[7:4]),
    .out_32(memoryrowdataconnector_1_out_32[3:0]), .in_18(shifter_1_out[6]), .in_19(shifter_1_out[5]),
    .in_20(shifter_1_out[4]), .in_21(shifter_1_out[3]), .in_22(shifter_1_out[2]), .in_23(shifter_1_out[1]),
    .in_24(shifter_1_out[0]));
  Shifter #(.shift("lr")) shifter_1 (.in(8'h80), .\dist (A[2:0]), .out(shifter_1_out));
  RAM #(.addrWidth(3), .dataWidth(32), .bus("separate")) ram_1 (
    .addr(A[5:3]), .din(memoryrowdataconnector_1_out_32), .data(out_6), .str(Write), .sel(1'b1), .clk(CLK),
    .clr(Reset));  // open: ld
  Multiplexer #(.select(3), .width(4)) multiplexer_1 (
    .in0(out_6[31:28]), .in1(out_6[27:24]), .in2(out_6[23:20]), .in3(out_6[19:16]), .in4(out_6[15:12]),
    .in5(out_6[11:8]), .in6(out_6[7:4]), .in7(out_6[3:0]), .out(out_7), .sel(A[2:0]));  // open: en

  // Notes on the sheet:
  //   Single room output
  //   Whole row of rooms output
endmodule
