// Logisim project test_alg2.circ as structural Verilog: 1 circuit, main circuit main
module main (
  input  [3:0] q,
  input  in_2,
  input  [7:0] Room_Limit,
  input  CLK,
  input  INIT,
  output [3:0] D,
  output [5:0] A,
  output W,
  output C,
  output R,
  output [5:0] SAFE_ROOM,
  output [7:0] Iteration,
  output IN_PROGRESS,
  output Finished
);

  wire and_1_out, and_2_out, and_3_out, and_4_out, and_5_out, and_6_out, and_7_out, AREG_CLK, AREG_RST,
       bitselector_1_out, comparator_2_eq, comparator_3_eq, comparator_4_gt, comparator_5_eq,
       comparator_6_eq, comparator_7_eq, CURRENT, Door_REG_CLK, Door_REG_RST, Flag, INIT_t, not_1_out,
       or_2_out, POP, PUSH, Que_CLK, RAM_REG_CLK, RAM_REG_RST, RAND_CLK, Room_Limit_t, Room_RAM_CLK,
       Room_RAM_RST, Room_RAM_VALUE;
  wire [1:0] DIRECTION, not_2_out;
  wire [3:0] Door_REG_VALUE, doordatagenerator_1_doors__inversed, Generate_correct_door_placement_doors,
       or_8_out, RAM_Data, RAM_REG_VALUE, RAND_VALUE;
  wire [5:0] AREG_VALUE, Choosen_Direction_s_Address_address_of_room_in_direction, multiplexer_1_out,
       multiplexer_2_out, Queue_output;
  wire [7:0] counter_1_q, Queue_Size, Room_Count;
  wire [13:3] rom_1_data;

  Random #(.width(6)) random_1 (.clk(and_1_out), .out(SAFE_ROOM));  // open: next, clr
  and and_1 (and_1_out, INIT, ~IN_PROGRESS);  // AND_Gate
  Comparator #(.mode("unsigned")) comparator_1 (.a(counter_1_q), .b(8'h3), .lt(INIT_t));  // open: gt, eq
  Comparator #(.mode("unsigned")) comparator_2 (.a(counter_1_q), .b(8'h3), .eq(comparator_2_eq));  // open: gt, lt
  Multiplexer #(.width(6), .enable("false")) multiplexer_1 (
    .in0(A), .in1(SAFE_ROOM), .out(multiplexer_1_out), .sel(INIT_t));
  D_Flip_Flop d_ff_1 (.clk(INIT), .D(1'b1), .Q(IN_PROGRESS), .reset(and_2_out));  // open: Qn, preset, en
  and and_2 (and_2_out, IN_PROGRESS, Finished);
  or or_1 (Finished, and_3_out, and_5_out);
  and and_3 (and_3_out, Room_Limit_t, comparator_2_eq);
  Comparator #(.mode("unsigned")) comparator_3 (.a(Queue_Size), .b({8{1'b0}}), .eq(comparator_3_eq));  // open: gt, lt
  Comparator #(.mode("unsigned")) comparator_4 (.a(Room_Count), .b(8'h1), .gt(comparator_4_gt));  // open: eq, lt
  FIFO_main Queue (
    .Input(multiplexer_1_out), .SIZE(Queue_Size), .PUSH(or_2_out), .POP(POP), .RST(INIT),
    .Output(Queue_output), .CLK(Que_CLK));  // open: FULL, EMPTY
  and and_4 (and_4_out, CLK, IN_PROGRESS, ~Finished);  // AND_Gate
  and and_5 (and_5_out, comparator_3_eq, comparator_4_gt);
  or or_2 (or_2_out, and_6_out, INIT_t);
  // roomLimit_main Room_Counter: pin names not known; wires that end beside it: or_2_out, Room_Limit, INIT, Room_Limit_t, Room_Count
  Counter #(.max('h2d)) counter_1 (
    .load(comparator_7_eq), .D(8'h3), .count(not_1_out), .Q(counter_1_q), .clk(and_4_out));  // open: carry, clr
  Comparator comparator_5 (.a(Queue_Size), .b({8{1'b0}}), .eq(comparator_5_eq));  // open: gt, lt
  and and_6 (and_6_out, PUSH, Flag);
  Comparator comparator_6 (.a(counter_1_q), .b(8'h3), .eq(comparator_6_eq));  // open: gt, lt
  Comparator comparator_7 (.a(counter_1_q), .b(8'h2d), .eq(comparator_7_eq));  // open: gt, lt
  not not_1 (not_1_out, comparator_7_eq);
  Multiplexer #(.width(6), .enable("false")) multiplexer_2 (
    .in0(Queue_output), .in1(SAFE_ROOM), .out(multiplexer_2_out), .sel(comparator_5_eq));
  Counter u_Iteration (.Q(Iteration), .clk(comparator_6_eq), .clr(INIT));  // open: load, D, count, carry
  LED led_1 (.in(RAND_VALUE[3]));
  LED led_2 ();  // open: in
  LED led_3 (.in(RAND_VALUE[0]));
  LED led_4 (.in(RAND_VALUE[1]));
  LED led_5 (.in(q[3]));
  LED led_6 ();  // open: in
  LED led_7 (.in(q[0]));
  LED led_8 (.in(q[1]));
  LED led_9 (.in(Door_REG_VALUE[3]));
  LED led_10 ();  // open: in
  LED led_11 (.in(Door_REG_VALUE[0]));
  LED led_12 (.in(Door_REG_VALUE[1]));
  LED led_13 (.in(RAM_REG_VALUE[3]));
  LED led_14 ();  // open: in
  LED led_15 (.in(RAM_REG_VALUE[0]));
  LED led_16 (.in(RAM_REG_VALUE[1]));
  LED led_17 (.in(Room_RAM_VALUE));
  Register #(.width(6)) Current_Address (
    .D(multiplexer_2_out), .Q(AREG_VALUE), .clk(AREG_CLK), .clr(AREG_RST));  // open: en
  ROM #(.dataWidth(18)) rom_1 (
    .addr(counter_1_q),
    .data({POP, PUSH, Que_CLK, AREG_CLK, rom_1_data[13], RAND_CLK, W, C, rom_1_data[9], Door_REG_CLK, rom_1_data[7], RAM_REG_CLK, rom_1_data[5], Room_RAM_CLK, rom_1_data[3], DIRECTION, CURRENT}));  // open: sel
  Hex_Digit_Display hex_digit_display_1 (.value(Queue_Size[7:4]));  // open: dp
  LED led_18 (.in(RAND_VALUE[2]));
  Hex_Digit_Display hex_digit_display_2 (.value({1'b0, AREG_VALUE[5:3]}));  // open: dp
  LED led_19 (.in(q[2]));
  Hex_Digit_Display hex_digit_display_3 (.value({1'b0, A[5:3]}));  // open: dp
  LED led_20 (.in(Door_REG_VALUE[2]));
  LED led_21 (.in(RAM_REG_VALUE[2]));
  Hex_Digit_Display hex_digit_display_4 (.value(Queue_Size[3:0]));  // open: dp
  Hex_Digit_Display hex_digit_display_5 (.value({1'b0, AREG_VALUE[2:0]}));  // open: dp
  Hex_Digit_Display hex_digit_display_6 (.value({1'b0, A[2:0]}));  // open: dp
  // doorChooser Room_Randomizer: pin names not known; wires that end beside it: AREG_VALUE, RAND_CLK, in_2, RAND_VALUE
  addressDirection Choosen_Direction_s_Address (
    .Direction(DIRECTION), .Address(AREG_VALUE),
    .Address_of_room_in_direction(Choosen_Direction_s_Address_address_of_room_in_direction));
  or or_3 (AREG_RST, rom_1_data[13], INIT);
  or or_4 (R, rom_1_data[9], INIT);
  or or_5 (Door_REG_RST, rom_1_data[7], INIT);
  or or_6 (RAM_REG_RST, rom_1_data[5], INIT);
  or or_7 (Room_RAM_RST, rom_1_data[3], INIT);
  assign or_8_out = RAM_REG_VALUE | Door_REG_VALUE;  // OR_Gate or_8, 4 bits wide
  Multiplexer #(.width(6), .enable("false")) multiplexer_3 (
    .in0(Choosen_Direction_s_Address_address_of_room_in_direction), .in1(AREG_VALUE), .out(A), .sel(CURRENT));
  Multiplexer #(.width(4), .enable("false")) multiplexer_4 (.in0(RAM_Data), .in1(or_8_out), .out(D), .sel(CURRENT));
  _64bitAddrReg Room_occupance_RAM (
    .Input(Flag), .RST(Room_RAM_RST), .Address(A), .CLK(and_7_out), .Output(Room_RAM_VALUE));
  and and_7 (and_7_out, Flag, Room_RAM_CLK);
  Register #(.width(4)) RAM_Value (.D(q), .Q(RAM_REG_VALUE), .clk(RAM_REG_CLK), .clr(RAM_REG_RST));  // open: en
  BitSelector #(.width(4)) bitselector_1 (.in(RAND_VALUE), .out(bitselector_1_out), .sel(not_2_out));
  assign not_2_out = ~DIRECTION;  // NOT_Gate not_2, 2 bits wide
  and and_8 (Flag, bitselector_1_out, ~Room_Limit_t, ~Room_RAM_VALUE);  // AND_Gate
  doorDataGenerator doordatagenerator_1 (
    .Input(Flag), .Direction(DIRECTION), .Doors__Inversed(doordatagenerator_1_doors__inversed));  // open: Doors
  doorDataGenerator Generate_correct_door_placement (
    .Input(Flag), .Direction(DIRECTION), .Doors(Generate_correct_door_placement_doors));  // open: Doors__Inversed
  _4BitAddrReg Current_Room_Doors (
    .Input(Generate_correct_door_placement_doors), .Address(DIRECTION), .CLK(Door_REG_CLK),
    ._0(Door_REG_RST), .Output(Door_REG_VALUE));
  assign RAM_Data = doordatagenerator_1_doors__inversed | RAM_REG_VALUE;  // OR_Gate or_9, 4 bits wide

  // Other names for the same wires on the sheet: RAM_CLK = C; RAM_Write = W; Counter_RST = INIT; Que_Reset = INIT;
  //   RAM_ADDRESS[5:0] = A; RAM_Reset = R; RAM_VALUE[3:0] = q

  // Notes on the sheet:
  //   contents of rom_1 (hex, n*v repeats v):
  //   0 8000 0 20a0 20000 25000 20000 140 10800 18c00 10800 20 10 0 2 142 10802 18c02 10802 22 12 2 4 144
  //   10804 18c04 10804 24 14 4 6 146 10806 18c06 10806 26 16 6 1 41 1 801 c01 20801 28000 20000
  //   Conditions to create a room
endmodule
