// Logisim project wybieracz_pokoi.circ as structural Verilog: 1 circuit, main circuit main
module main (
  input  in_1,
  output [2:0] out_2
);

  wire comparator_1_gt;

  Counter #(.width(3), .max('h7)) counter_1 (
    .Q(out_2), .clk(in_1), .clr(comparator_1_gt));  // open: load, D, count, carry
  Comparator #(.width(3), .mode("unsigned")) comparator_1 (
    .a(out_2), .b(3'b100), .gt(comparator_1_gt));  // open: eq, lt
endmodule
